// Logisim project CPU.circ as structural Verilog
module CPU (
  input  [3:0] mul2_constant,
  input  [7:0] mul1_register,
  input  in_3,
  input  in_4,
  input  in_5,
  input  in_6,
  input  in_7,
  input  in_8,
  input  in_9,
  input  in_10,
  input  in_11,
  input  in_12,
  output [7:0] out_13,
  output [7:0] out_14,
  output [7:0] out_15,
  output [7:0] out_16,
  output [7:0] out_17,
  output [11:0] out_18,
  output overflow_error_3f72c512
);

  wire ADD_2_out, add_out, and_1_out, and_2_out, and_3_out, and_4_out, and_5_out, and_6_out, and_7_out,
       and_8_out, and_9_out, and_10_out, and_11_out, and_12_out, and_13_out, and_14_out, and_15_out,
       and_16_out, and_17_out, and_18_out, and_19_out, and_20_out, and_21_out, and_22_out, and_23_out,
       BEQ_out, BNQ_out, clock_1_out, clock_2_out, DRread_out, eight_out, five_out, four_out,
       hexadigit_1_out_2, hexadigit_1_out_3, hexadigit_1_out_4, hexadigit_1_out_5, hexadigit_1_out_6,
       hexadigit_1_out_7, hexadigit_1_out_8, hexadigit_2_out_2, hexadigit_2_out_3, hexadigit_2_out_4,
       hexadigit_2_out_5, hexadigit_2_out_6, hexadigit_2_out_7, hexadigit_2_out_8, hexadigit_3_out_2,
       hexadigit_3_out_3, hexadigit_3_out_4, hexadigit_3_out_5, hexadigit_3_out_6, hexadigit_3_out_7,
       hexadigit_3_out_8, input_to_0_1_out, input_to_0_2_out, input_to_1_1_out, input_to_1_2_out,
       inputToD0_out, inputToD1_out, LoadRAMToD0_out, LoadRAMToD1_out, muld0_1_out, muld0_2_out, muld1_1_out,
       muld1_2_out, multiplexer_6_out, multiply_d0_out, multiply_d1_out, multiply_rom_out, nine_out,
       not_1_out, not_2_out, not_3_out, not_4_out, not_5_out, not_6_out, not_7_out, not_8_out, not_9_out,
       not_10_out, not_11_out, not_12_out, not_13_out, not_14_out, not_15_out, not_16_out, not_17_out,
       not_18_out, not_19_out, not_20_out, not_21_out, not_22_out, not_23_out, not_24_out, not_25_out,
       not_26_out, not_27_out, not_28_out, not_29_out, not_30_out, not_31_out, not_32_out, not_33_out,
       not_34_out, not_35_out, not_36_out, not_37_out, not_38_out, not_39_out, not_40_out, not_41_out,
       not_42_out, not_43_out, not_44_out, not_45_out, not_46_out, not_47_out, not_48_out, not_49_out,
       not_50_out, not_51_out, not_52_out, not_53_out, not_54_out, not_55_out, not_56_out, not_57_out,
       not_58_out, not_59_out, not_60_out, not_61_out, not_62_out, on_off_switch_out, one_out, openD0_out,
       openMBR_out, or_1_out, or_2_out, or_3_out, or_4_out, or_6_out, or_7_out, or_9_out, or_10_out,
       or_11_out, or_14_out, or_15_out, or_16_out, or_17_out, or_18_out, or_19_out, or_20_out, or_21_out,
       or_22_out, or_23_out, or_24_out, or_25_out, or_26_out, or_27_out, or_28_out, or_29_out, or_30_out,
       or_31_out, or_32_out, or_33_out, or_34_out, PrintD0_out, PrintD1_out, program_rom_out, seven_out,
       six_out, Status_overflow, Status_zero, STOP_out, Store_out, StoreD0ToRam_out, StoreD1ToRam_out,
       SubD0D1_out, SubD1D0_out, ten_out, three_out, two_out, Zero_out;
  wire [1:0] or_5_out, or_12_out;
  wire [2:0] ALU_out_4;
  wire [3:0] Address_Register_addr_out, count_1_out, inc_1_r, inc_2_r, MAR_addr_out, multiplexer_4_out,
       multiplexer_7_out, PC_addr_out;
  wire [7:0] ALU_output, const__data_out, D0_data_out, D1_data_out, Data_Register_data_out,
       inputbuffer_1_out_14, IR_data_out, L_data_out, MBR_data_out, multiplexer_1_out, multiplexer_2_out,
       multiplexer_3_out, multiplexer_5_out, multiply_ALU__out_put, R_data_out, ram_1_ram_out,
       regnumber__data_out;

  Button program_rom (.out(program_rom_out));
  Button on_off_switch (.out(on_off_switch_out));
  Button multiply_rom (.out(multiply_rom_out));
  Multiplexer #(.width(8), .enable("false")) multiplexer_1 (
    .in0(Data_Register_data_out), .in1(inputbuffer_1_out_14), .out(multiplexer_1_out), .sel(or_19_out));
  inputbuffer inputbuffer_1 (
    .RW(or_18_out), .out_13(out_14), .out_14(inputbuffer_1_out_14), .CLK(clock_1_out), .one(in_3),
    .two(in_4), .three(in_5), .four(in_6), .five(in_7), .six(in_8), .seven(in_9), .eight(in_10),
    .nine(in_11), .zero(in_12));
  _7_Segment_Display u_7_segment_display_1 (
    .g(hexadigit_1_out_8), .f(hexadigit_1_out_7), .a(hexadigit_1_out_2), .b(hexadigit_1_out_3),
    .e(hexadigit_1_out_6), .d(hexadigit_1_out_5), .c(hexadigit_1_out_4));  // open: dp
  hexadigit hexadigit_1 (
    .in_1(out_18[11:8]), .out_2(hexadigit_1_out_2), .out_3(hexadigit_1_out_3), .out_4(hexadigit_1_out_4),
    .out_5(hexadigit_1_out_5), .out_6(hexadigit_1_out_6), .out_7(hexadigit_1_out_7), .out_8(hexadigit_1_out_8));
  or or_1 (or_1_out, two_out, and_9_out, DRread_out);
  hexadigit hexadigit_2 (
    .in_1(out_18[7:4]), .out_2(hexadigit_2_out_2), .out_3(hexadigit_2_out_3), .out_4(hexadigit_2_out_4),
    .out_5(hexadigit_2_out_5), .out_6(hexadigit_2_out_6), .out_7(hexadigit_2_out_7), .out_8(hexadigit_2_out_8));
  // Probe on mul2_constant
  // Probe on mul1_register
  DR Data_Register (
    .readwrite(or_1_out), .clk(clock_1_out), .DATA_OUT(Data_Register_data_out), .out_5(out_13),
    .IN(multiplexer_2_out), .on_off_switch(on_off_switch_out));
  AR Address_Register (
    .PC_IN(MAR_addr_out), .ADDR_OUT(Address_Register_addr_out), .CU_CONTROL(or_2_out), .CLK(clock_1_out));  // open: out_4
  or or_2 (or_2_out, one_out, and_9_out, and_6_out);
  _7_Segment_Display u_7_segment_display_2 (
    .g(hexadigit_2_out_8), .f(hexadigit_2_out_7), .a(hexadigit_2_out_2), .b(hexadigit_2_out_3),
    .e(hexadigit_2_out_6), .d(hexadigit_2_out_5), .c(hexadigit_2_out_4));  // open: dp
  hexadigit hexadigit_3 (
    .in_1(out_18[3:0]), .out_2(hexadigit_3_out_2), .out_3(hexadigit_3_out_3), .out_4(hexadigit_3_out_4),
    .out_5(hexadigit_3_out_5), .out_6(hexadigit_3_out_6), .out_7(hexadigit_3_out_7), .out_8(hexadigit_3_out_8));
  Clock clock_1 (.out(clock_1_out));
  RAM ram_1 (
    .ADDR_IN(Address_Register_addr_out), .DATA_IN(Data_Register_data_out), .CLK(clock_1_out),
    .RAM_OUT(ram_1_ram_out), .RW(and_10_out), .program_rom(program_rom_out),
    .on_off_switch(on_off_switch_out), .multiply_rom(multiply_rom_out), .mul1_constant(mul2_constant),
    .mul2(mul1_register));  // open: out_10
  Multiplexer #(.width(8), .enable("false")) multiplexer_2 (
    .in0(ram_1_ram_out), .in1(MBR_data_out), .out(multiplexer_2_out), .sel(and_9_out));
  DR dr_1 (
    .readwrite(and_19_out), .clk(clock_1_out), .DATA_OUT(out_15), .IN(MBR_data_out),
    .on_off_switch(on_off_switch_out));  // open: out_5
  switch_to_decimal switch_to_decimal_1 (.in_1(out_15), .out_2(out_18));
  _7_Segment_Display u_7_segment_display_3 (
    .g(hexadigit_3_out_8), .f(hexadigit_3_out_7), .a(hexadigit_3_out_2), .b(hexadigit_3_out_3),
    .e(hexadigit_3_out_6), .d(hexadigit_3_out_5), .c(hexadigit_3_out_4));  // open: dp
  or or_3 (or_3_out, Store_out, and_5_out, Zero_out);
  MAR_6e5ae79d MAR (
    .CU_CONTROL(or_3_out), .CLK(clock_2_out), .PC_IN(multiplexer_4_out), .ADDR_OUT(MAR_addr_out));  // open: out_4
  DR MBR (
    .readwrite(or_4_out), .clk(clock_1_out), .DATA_OUT(MBR_data_out), .IN(multiplexer_5_out),
    .on_off_switch(on_off_switch_out));  // open: out_5
  or or_4 (or_4_out, and_8_out, three_out, and_11_out, or_19_out, openMBR_out, and_20_out, and_18_out);
  Multiplexer #(.select(2), .width(8), .enable("false")) multiplexer_3 (
    .in0(MBR_data_out), .in1(ALU_output), .in2(multiply_ALU__out_put), .out(multiplexer_3_out), .sel(or_5_out));  // open: in3
  or or_5 (or_5_out[0], and_16_out, and_13_out);
  Multiplexer #(.width(4), .enable("false")) multiplexer_4 (
    .in0(PC_addr_out), .in1(IR_data_out[3:0]), .out(multiplexer_4_out), .sel(or_6_out));
  or or_6 (or_6_out, Store_out, on_off_switch_out, and_5_out);
  Multiplexer #(.select(2), .width(8), .enable("false")) multiplexer_5 (
    .in0(multiplexer_1_out), .in1(D0_data_out), .in2(D1_data_out), .out(multiplexer_5_out), .sel(or_12_out));  // open: in3
  and and_1 (and_1_out, and_13_out, not_2_out);
  or or_7 (or_7_out, muld0_2_out, and_1_out, and_22_out, openD0_out);
  DR D0 (
    .readwrite(or_7_out), .clk(clock_1_out), .DATA_OUT(D0_data_out), .out_5(out_16), .IN(multiplexer_3_out),
    .on_off_switch(on_off_switch_out));
  or or_8 (or_5_out[1], muld0_2_out, muld1_2_out);
  or or_9 (or_9_out, STOP_out, on_off_switch_out);
  INC inc_1 (.A(PC_addr_out), .in_2(or_9_out), .R(inc_1_r));
  AR PC (.PC_IN(multiplexer_7_out), .ADDR_OUT(PC_addr_out), .CU_CONTROL(or_10_out), .CLK(clock_2_out));  // open: out_4
  or or_10 (or_10_out, multiplexer_6_out, five_out);
  DR IR (
    .readwrite(four_out), .clk(clock_2_out), .DATA_OUT(IR_data_out), .IN(MBR_data_out),
    .on_off_switch(on_off_switch_out));  // open: out_5
  Multiplexer #(.enable("false")) multiplexer_6 (
    .in0(and_3_out), .in1(not_1_out), .out(multiplexer_6_out), .sel(and_4_out));
  not not_1 (not_1_out, and_3_out);
  not not_2 (not_2_out, IR_data_out[0]);
  and and_2 (and_2_out, and_13_out, IR_data_out[0]);
  or or_11 (or_11_out, and_7_out, and_2_out, or_15_out, and_16_out);
  DR D1 (
    .readwrite(or_11_out), .clk(clock_1_out), .DATA_OUT(D1_data_out), .out_5(out_17), .IN(multiplexer_3_out),
    .on_off_switch(on_off_switch_out));
  Multiplexer #(.width(4), .enable("false")) multiplexer_7 (
    .in0(inc_1_r), .in1(IR_data_out[3:0]), .out(multiplexer_7_out), .sel(multiplexer_6_out));
  or or_12 (or_12_out[0], muld0_1_out, and_8_out, add_out, and_18_out, and_15_out);
  or or_13 (or_12_out[1], muld1_1_out, and_11_out, and_20_out, and_14_out, and_12_out);
  ALU_43ff114b ALU (.Add1SUB0(ADD_2_out), .out_4(ALU_out_4), .OUTPUT(ALU_output), .L(R_data_out), .R(L_data_out));
  DR L (
    .readwrite(or_14_out), .clk(clock_1_out), .DATA_OUT(L_data_out), .IN(multiplexer_5_out),
    .on_off_switch(on_off_switch_out));  // open: out_5
  or or_14 (or_14_out, and_14_out, add_out);
  or or_15 (or_15_out, muld1_2_out, and_23_out);
  DR R (
    .readwrite(or_16_out), .clk(clock_1_out), .DATA_OUT(R_data_out), .IN(multiplexer_5_out),
    .on_off_switch(on_off_switch_out));  // open: out_5
  or or_16 (or_16_out, and_15_out, and_12_out);
  Status Status (
    .in_1(ALU_out_4), .CLK(clock_1_out), .ReadWrite(and_21_out), .zero(Status_zero),
    .overflow(Status_overflow));  // open: negative, out_4
  and and_3 (and_3_out, Status_zero, not_3_out, and_17_out);
  not not_3 (not_3_out, Status_overflow);
  DR const_ (
    .readwrite(or_20_out), .clk(clock_1_out), .DATA_OUT(const__data_out), .IN({4'b0000, IR_data_out[3:0]}));  // open: out_5, on_off_switch
  DR regnumber_ (
    .readwrite(or_20_out), .clk(clock_1_out), .DATA_OUT(regnumber__data_out), .IN(multiplexer_5_out));  // open: out_5, on_off_switch
  INC inc_2 (.A(count_1_out), .in_2(or_17_out), .R(inc_2_r));
  or or_17 (or_17_out, on_off_switch_out, STOP_out);
  Count count_1 (.IN(inc_2_r), .CLK(clock_2_out), .OUT(count_1_out));
  and and_4 (and_4_out, BNQ_out, and_17_out);
  and and_5 (and_5_out, or_21_out, six_out);
  and and_6 (and_6_out, or_22_out, seven_out);
  and DRread (DRread_out, or_23_out, eight_out);
  and openMBR (openMBR_out, or_24_out, nine_out);
  and openD0 (openD0_out, LoadRAMToD0_out, ten_out);
  and and_7 (and_7_out, LoadRAMToD1_out, ten_out);
  and Store (Store_out, or_25_out, six_out);
  and and_8 (and_8_out, StoreD0ToRam_out, seven_out);
  and and_9 (and_9_out, or_26_out, eight_out);
  and and_10 (and_10_out, or_27_out, nine_out);
  and and_11 (and_11_out, StoreD1ToRam_out, seven_out);
  and add (add_out, or_28_out, six_out);
  and and_12 (and_12_out, or_29_out, seven_out);
  and and_13 (and_13_out, or_30_out, eight_out);
  and and_14 (and_14_out, or_31_out, six_out);
  and and_15 (and_15_out, or_32_out, seven_out);
  and and_16 (and_16_out, SubD1D0_out, eight_out);
  and and_17 (and_17_out, or_34_out, nine_out);
  and input_to_0_1 (input_to_0_1_out, inputToD0_out, six_out);
  or or_18 (or_18_out, input_to_0_1_out, input_to_1_1_out);
  and input_to_1_1 (input_to_1_1_out, inputToD1_out, six_out);
  and input_to_0_2 (input_to_0_2_out, inputToD0_out, seven_out);
  or or_19 (or_19_out, input_to_0_2_out, input_to_1_2_out);
  and input_to_1_2 (input_to_1_2_out, inputToD1_out, seven_out);
  and and_18 (and_18_out, PrintD0_out, six_out);
  and and_19 (and_19_out, or_33_out, seven_out);
  and and_20 (and_20_out, PrintD1_out, six_out);
  and and_21 (and_21_out, or_34_out, eight_out);
  and and_22 (and_22_out, inputToD0_out, eight_out);
  and and_23 (and_23_out, inputToD1_out, eight_out);
  and muld0_1 (muld0_1_out, multiply_d0_out, six_out);
  and muld0_2 (muld0_2_out, multiply_d0_out, seven_out);
  and muld1_1 (muld1_1_out, multiply_d1_out, six_out);
  and muld1_2 (muld1_2_out, multiply_d1_out, seven_out);
  or or_20 (or_20_out, muld0_1_out, muld1_1_out);
  not not_4 (not_4_out, IR_data_out[7]);
  or or_21 (or_21_out, LoadRAMToD0_out, LoadRAMToD1_out);
  or or_22 (or_22_out, LoadRAMToD0_out, LoadRAMToD1_out);
  or or_23 (or_23_out, LoadRAMToD0_out, LoadRAMToD1_out);
  or or_24 (or_24_out, LoadRAMToD0_out, LoadRAMToD1_out);
  or or_25 (or_25_out, StoreD0ToRam_out, StoreD1ToRam_out);
  or or_26 (or_26_out, StoreD0ToRam_out, StoreD1ToRam_out);
  or or_27 (or_27_out, StoreD0ToRam_out, StoreD1ToRam_out);
  or or_28 (or_28_out, ADD_2_out, SubD0D1_out);
  or or_29 (or_29_out, ADD_2_out, SubD0D1_out);
  or or_30 (or_30_out, ADD_2_out, SubD0D1_out);
  or or_31 (or_31_out, SubD1D0_out, or_34_out);
  or or_32 (or_32_out, SubD1D0_out, or_34_out);
  or or_33 (or_33_out, PrintD0_out, PrintD1_out);
  Clock clock_2 (.out(clock_2_out));
  not not_5 (not_5_out, IR_data_out[4]);
  not not_6 (not_6_out, IR_data_out[6]);
  not not_7 (not_7_out, IR_data_out[5]);
  not not_8 (not_8_out, IR_data_out[6]);
  not not_9 (not_9_out, IR_data_out[7]);
  and LoadRAMToD1 (LoadRAMToD1_out, not_9_out, not_8_out, not_12_out, IR_data_out[4]);
  and LoadRAMToD0 (LoadRAMToD0_out, not_4_out, not_6_out, not_7_out, not_5_out);
  not not_10 (not_10_out, IR_data_out[6]);
  not not_11 (not_11_out, IR_data_out[4]);
  not not_12 (not_12_out, IR_data_out[5]);
  not not_13 (not_13_out, IR_data_out[7]);
  and StoreD0ToRam (StoreD0ToRam_out, not_13_out, not_10_out, IR_data_out[5], not_11_out);
  not not_14 (not_14_out, IR_data_out[7]);
  not not_15 (not_15_out, IR_data_out[6]);
  not not_16 (not_16_out, IR_data_out[7]);
  and StoreD1ToRam (StoreD1ToRam_out, not_16_out, not_15_out, IR_data_out[5], IR_data_out[4]);
  multiply_ALU multiply_ALU_ (
    .\const (const__data_out), .regnumber(regnumber__data_out), .out_put(multiply_ALU__out_put),
    .overflow_error(overflow_error_3f72c512));
  not not_17 (not_17_out, IR_data_out[7]);
  not not_18 (not_18_out, IR_data_out[4]);
  not not_19 (not_19_out, IR_data_out[5]);
  and SubD0D1 (SubD0D1_out, not_17_out, IR_data_out[6], not_22_out, IR_data_out[4]);
  and ADD_2 (ADD_2_out, not_14_out, IR_data_out[6], not_19_out, not_18_out);
  not not_20 (not_20_out, IR_data_out[7]);
  not not_21 (not_21_out, IR_data_out[4]);
  not not_22 (not_22_out, IR_data_out[5]);
  and SubD1D0 (SubD1D0_out, not_20_out, IR_data_out[6], IR_data_out[5], not_21_out);
  not not_23 (not_23_out, IR_data_out[7]);
  and BEQ (BEQ_out, not_23_out, IR_data_out[6], IR_data_out[5], IR_data_out[4]);
  or or_34 (or_34_out, BEQ_out, BNQ_out);
  not not_24 (not_24_out, IR_data_out[6]);
  not not_25 (not_25_out, IR_data_out[4]);
  not not_26 (not_26_out, IR_data_out[5]);
  not not_27 (not_27_out, IR_data_out[6]);
  and inputToD0 (inputToD0_out, IR_data_out[7], not_27_out, not_29_out, IR_data_out[4]);
  and BNQ (BNQ_out, IR_data_out[7], not_24_out, not_26_out, not_25_out);
  not not_28 (not_28_out, IR_data_out[4]);
  not not_29 (not_29_out, IR_data_out[5]);
  not not_30 (not_30_out, IR_data_out[6]);
  and inputToD1 (inputToD1_out, IR_data_out[7], not_30_out, IR_data_out[5], not_28_out);
  not not_31 (not_31_out, IR_data_out[6]);
  and PrintD0 (PrintD0_out, IR_data_out[7], not_31_out, IR_data_out[5], IR_data_out[4]);
  not not_32 (not_32_out, IR_data_out[4]);
  not not_33 (not_33_out, IR_data_out[5]);
  and PrintD1 (PrintD1_out, IR_data_out[7], IR_data_out[6], not_33_out, not_32_out);
  and STOP (STOP_out, IR_data_out[7], IR_data_out[6], not_34_out, IR_data_out[4]);
  not not_34 (not_34_out, IR_data_out[5]);
  not not_35 (not_35_out, IR_data_out[4]);
  and multiply_d0 (multiply_d0_out, IR_data_out[7], IR_data_out[6], IR_data_out[5], not_35_out);
  and multiply_d1 (multiply_d1_out, IR_data_out[7], IR_data_out[6], IR_data_out[5], IR_data_out[4]);
  not not_36 (not_36_out, count_1_out[3]);
  not not_37 (not_37_out, count_1_out[2]);
  not not_38 (not_38_out, count_1_out[1]);
  not not_39 (not_39_out, count_1_out[3]);
  not not_40 (not_40_out, count_1_out[0]);
  and Zero (Zero_out, not_36_out, not_37_out, not_38_out, not_40_out);
  not not_41 (not_41_out, count_1_out[2]);
  not not_42 (not_42_out, count_1_out[1]);
  not not_43 (not_43_out, count_1_out[3]);
  not not_44 (not_44_out, count_1_out[2]);
  and two (two_out, not_43_out, not_44_out, count_1_out[1], not_45_out);
  and one (one_out, not_39_out, not_41_out, not_42_out, count_1_out[0]);
  not not_45 (not_45_out, count_1_out[0]);
  not not_46 (not_46_out, count_1_out[2]);
  not not_47 (not_47_out, count_1_out[3]);
  and three (three_out, not_47_out, not_46_out, count_1_out[1], count_1_out[0]);
  not not_48 (not_48_out, count_1_out[3]);
  not not_49 (not_49_out, count_1_out[0]);
  not not_50 (not_50_out, count_1_out[1]);
  not not_51 (not_51_out, count_1_out[3]);
  and four (four_out, not_48_out, count_1_out[2], not_50_out, not_49_out);
  not not_52 (not_52_out, count_1_out[3]);
  not not_53 (not_53_out, count_1_out[1]);
  and five (five_out, not_51_out, count_1_out[2], not_53_out, count_1_out[0]);
  and six (six_out, not_52_out, count_1_out[2], count_1_out[1], not_55_out);
  not not_54 (not_54_out, count_1_out[3]);
  not not_55 (not_55_out, count_1_out[0]);
  and seven (seven_out, not_54_out, count_1_out[2], count_1_out[1], count_1_out[0]);
  not not_56 (not_56_out, count_1_out[2]);
  not not_57 (not_57_out, count_1_out[1]);
  not not_58 (not_58_out, count_1_out[0]);
  and eight (eight_out, count_1_out[3], not_56_out, not_57_out, not_58_out);
  not not_59 (not_59_out, count_1_out[2]);
  not not_60 (not_60_out, count_1_out[1]);
  not not_61 (not_61_out, count_1_out[2]);
  and ten (ten_out, count_1_out[3], not_61_out, count_1_out[1], not_62_out);
  and nine (nine_out, count_1_out[3], not_59_out, not_60_out, count_1_out[0]);
  not not_62 (not_62_out, count_1_out[0]);

  // Notes on the sheet:
  //   Counter
endmodule

module RAM (
  input  [3:0] ADDR_IN,
  input  [7:0] DATA_IN,
  input  [3:0] mul1_constant,
  input  RW,
  input  CLK,
  input  [7:0] mul2,
  input  program_rom,
  input  on_off_switch,
  input  multiply_rom,
  output [7:0] out_10,
  output [7:0] RAM_OUT
);

  wire and_1_out, and_2_out, and_3_out, and_4_out, and_5_out, and_6_out, and_7_out, and_8_out, and_9_out,
       and_10_out, and_11_out, and_12_out, and_13_out, and_14_out, and_15_out, and_16_out, not_1_out,
       not_2_out, not_3_out, not_4_out, not_5_out, not_6_out, not_7_out, not_8_out, not_9_out, not_10_out,
       not_11_out, not_12_out, not_13_out, not_14_out, not_15_out, not_16_out, not_17_out, not_18_out,
       not_19_out, not_20_out, not_21_out, not_22_out, not_23_out, not_24_out, not_25_out, not_26_out,
       not_27_out, not_28_out, not_29_out, not_30_out, not_31_out, not_32_out, not_33_out;
  wire [7:0] byte1_bit1, byte2_bit1, byte3_bit1, byte4_bit1, byte5_bit1, byte6_bit1, byte7_bit1, byte8_bit1,
       byte9_bit1, byte10_bit1, byte11_bit1, byte12_bit1, byte13_bit1, byte14_bit1, byte15_bit1, byte16_bit1,
       multiplexer_1_out, multiplexer_2_out, multiplexer_3_out, multiplexer_4_out, multiplexer_5_out,
       multiplexer_6_out, multiplexer_7_out, multiplexer_8_out, multiplexer_9_out, multiplexer_10_out,
       multiplexer_11_out, multiplexer_12_out, multiplexer_13_out, multiplexer_14_out, multiplexer_15_out,
       multiplexer_16_out, multiplexer_17_out, multiplexer_18_out, multiplexer_19_out, multiplexer_20_out,
       multiplexer_21_out, multiplexer_22_out, multiplexer_23_out, multiplexer_24_out, multiplexer_25_out,
       multiplexer_26_out, multiplexer_27_out, multiplexer_28_out, multiplexer_29_out, multiplexer_30_out,
       multiplexer_31_out, multiplexer_32_out, multiplexer_33_out, multiplexer_34_out, multiplexer_35_out,
       multiplexer_36_out, multiplexer_37_out, or_1_out, or_2_out, or_3_out, or_4_out, or_6_out;

  not not_1 (not_1_out, RW);
  not not_2 (not_2_out, ADDR_IN[3]);
  not not_3 (not_3_out, ADDR_IN[2]);
  not not_4 (not_4_out, ADDR_IN[1]);
  not not_5 (not_5_out, ADDR_IN[0]);
  not not_6 (not_6_out, ADDR_IN[3]);
  not not_7 (not_7_out, ADDR_IN[2]);
  not not_8 (not_8_out, ADDR_IN[1]);
  not not_9 (not_9_out, ADDR_IN[3]);
  not not_10 (not_10_out, ADDR_IN[2]);
  not not_11 (not_11_out, ADDR_IN[0]);
  not not_12 (not_12_out, ADDR_IN[3]);
  not not_13 (not_13_out, ADDR_IN[2]);
  not not_14 (not_14_out, ADDR_IN[3]);
  not not_15 (not_15_out, ADDR_IN[1]);
  not not_16 (not_16_out, ADDR_IN[0]);
  not not_17 (not_17_out, ADDR_IN[3]);
  not not_18 (not_18_out, ADDR_IN[1]);
  not not_19 (not_19_out, ADDR_IN[3]);
  not not_20 (not_20_out, ADDR_IN[0]);
  not not_21 (not_21_out, ADDR_IN[3]);
  not not_22 (not_22_out, ADDR_IN[2]);
  not not_23 (not_23_out, ADDR_IN[1]);
  not not_24 (not_24_out, ADDR_IN[0]);
  not not_25 (not_25_out, ADDR_IN[2]);
  not not_26 (not_26_out, ADDR_IN[1]);
  not not_27 (not_27_out, ADDR_IN[2]);
  not not_28 (not_28_out, ADDR_IN[0]);
  not not_29 (not_29_out, ADDR_IN[2]);
  not not_30 (not_30_out, ADDR_IN[1]);
  not not_31 (not_31_out, ADDR_IN[0]);
  not not_32 (not_32_out, ADDR_IN[1]);
  not not_33 (not_33_out, ADDR_IN[0]);
  and and_1 (and_1_out, not_2_out, not_3_out, not_4_out, not_5_out);
  and and_2 (and_2_out, not_6_out, not_7_out, not_8_out, ADDR_IN[0]);
  and and_3 (and_3_out, not_9_out, not_10_out, ADDR_IN[1], not_11_out);
  and and_4 (and_4_out, not_12_out, not_13_out, ADDR_IN[1], ADDR_IN[0]);
  and and_5 (and_5_out, not_14_out, ADDR_IN[2], not_15_out, not_16_out);
  and and_6 (and_6_out, not_17_out, ADDR_IN[2], not_18_out, ADDR_IN[0]);
  and and_7 (and_7_out, not_19_out, ADDR_IN[2], ADDR_IN[1], not_20_out);
  and and_8 (and_8_out, not_21_out, ADDR_IN[2], ADDR_IN[1], ADDR_IN[0]);
  and and_9 (and_9_out, ADDR_IN[3], not_22_out, not_23_out, not_24_out);
  and and_10 (and_10_out, ADDR_IN[3], not_25_out, not_26_out, ADDR_IN[0]);
  and and_11 (and_11_out, ADDR_IN[3], not_27_out, ADDR_IN[1], not_28_out);
  and and_12 (and_12_out, ADDR_IN[3], not_29_out, ADDR_IN[1], ADDR_IN[0]);
  and and_13 (and_13_out, ADDR_IN[3], ADDR_IN[2], not_30_out, not_31_out);
  and and_14 (and_14_out, ADDR_IN[3], ADDR_IN[2], not_32_out, ADDR_IN[0]);
  and and_15 (and_15_out, ADDR_IN[3], ADDR_IN[2], ADDR_IN[1], not_33_out);
  and and_16 (and_16_out, ADDR_IN[3], ADDR_IN[2], ADDR_IN[1], ADDR_IN[0]);
  ram byte1 (
    .READWRITE(not_1_out), .ADDR(and_1_out), .CLK(CLK), .bit1(byte1_bit1[0]), .bit2(byte1_bit1[1]),
    .bit3(byte1_bit1[2]), .bit4(byte1_bit1[3]), .input1(DATA_IN[0]), .input2(DATA_IN[1]),
    .input3(DATA_IN[2]), .input4(DATA_IN[3]), .out_14(out_10[0]), .out_15(out_10[1]), .out_16(out_10[2]),
    .out_17(out_10[3]), .bit5(byte1_bit1[4]), .bit6(byte1_bit1[5]), .bit7(byte1_bit1[6]),
    .bit8(byte1_bit1[7]), .input6(DATA_IN[5]), .input7(DATA_IN[6]), .input8(DATA_IN[7]), .input5(DATA_IN[4]),
    .out_18(out_10[4]), .out_19(out_10[5]), .out_20(out_10[6]), .out_21(out_10[7]), .ROMON(or_1_out),
    .RAMOUT(multiplexer_2_out));
  ram byte2 (
    .READWRITE(not_1_out), .ADDR(and_2_out), .CLK(CLK), .bit1(byte2_bit1[0]), .bit2(byte2_bit1[1]),
    .bit3(byte2_bit1[2]), .bit4(byte2_bit1[3]), .input1(DATA_IN[0]), .input2(DATA_IN[1]),
    .input3(DATA_IN[2]), .input4(DATA_IN[3]), .bit5(byte2_bit1[4]), .bit6(byte2_bit1[5]),
    .bit7(byte2_bit1[6]), .bit8(byte2_bit1[7]), .input6(DATA_IN[5]), .input7(DATA_IN[6]),
    .input8(DATA_IN[7]), .input5(DATA_IN[4]), .ROMON(or_2_out), .RAMOUT(multiplexer_5_out));  // open: out_14, out_15, out_16, out_17, out_18, out_19, out_20, out_21
  ram byte3 (
    .READWRITE(not_1_out), .ADDR(and_3_out), .CLK(CLK), .bit1(byte3_bit1[0]), .bit2(byte3_bit1[1]),
    .bit3(byte3_bit1[2]), .bit4(byte3_bit1[3]), .input1(DATA_IN[0]), .input2(DATA_IN[1]),
    .input3(DATA_IN[2]), .input4(DATA_IN[3]), .bit5(byte3_bit1[4]), .bit6(byte3_bit1[5]),
    .bit7(byte3_bit1[6]), .bit8(byte3_bit1[7]), .input6(DATA_IN[5]), .input7(DATA_IN[6]),
    .input8(DATA_IN[7]), .input5(DATA_IN[4]), .ROMON(or_3_out), .RAMOUT(multiplexer_8_out));  // open: out_14, out_15, out_16, out_17, out_18, out_19, out_20, out_21
  ram byte4 (
    .READWRITE(not_1_out), .ADDR(and_4_out), .CLK(CLK), .bit1(byte4_bit1[0]), .bit2(byte4_bit1[1]),
    .bit3(byte4_bit1[2]), .bit4(byte4_bit1[3]), .input1(DATA_IN[0]), .input2(DATA_IN[1]),
    .input3(DATA_IN[2]), .input4(DATA_IN[3]), .bit5(byte4_bit1[4]), .bit6(byte4_bit1[5]),
    .bit7(byte4_bit1[6]), .bit8(byte4_bit1[7]), .input6(DATA_IN[5]), .input7(DATA_IN[6]),
    .input8(DATA_IN[7]), .input5(DATA_IN[4]), .ROMON(or_6_out), .RAMOUT(multiplexer_10_out));  // open: out_14, out_15, out_16, out_17, out_18, out_19, out_20, out_21
  ram byte5 (
    .READWRITE(not_1_out), .ADDR(and_5_out), .CLK(CLK), .bit1(byte5_bit1[0]), .bit2(byte5_bit1[1]),
    .bit3(byte5_bit1[2]), .bit4(byte5_bit1[3]), .input1(DATA_IN[0]), .input2(DATA_IN[1]),
    .input3(DATA_IN[2]), .input4(DATA_IN[3]), .bit5(byte5_bit1[4]), .bit6(byte5_bit1[5]),
    .bit7(byte5_bit1[6]), .bit8(byte5_bit1[7]), .input6(DATA_IN[5]), .input7(DATA_IN[6]),
    .input8(DATA_IN[7]), .input5(DATA_IN[4]), .ROMON(multiplexer_14_out), .RAMOUT(multiplexer_13_out));  // open: out_14, out_15, out_16, out_17, out_18, out_19, out_20, out_21
  ram byte6 (
    .READWRITE(not_1_out), .ADDR(and_6_out), .CLK(CLK), .bit1(byte6_bit1[0]), .bit2(byte6_bit1[1]),
    .bit3(byte6_bit1[2]), .bit4(byte6_bit1[3]), .input1(DATA_IN[0]), .input2(DATA_IN[1]),
    .input3(DATA_IN[2]), .input4(DATA_IN[3]), .bit5(byte6_bit1[4]), .bit6(byte6_bit1[5]),
    .bit7(byte6_bit1[6]), .bit8(byte6_bit1[7]), .input6(DATA_IN[5]), .input7(DATA_IN[6]),
    .input8(DATA_IN[7]), .input5(DATA_IN[4]), .ROMON(multiplexer_16_out), .RAMOUT(multiplexer_15_out));  // open: out_14, out_15, out_16, out_17, out_18, out_19, out_20, out_21
  ram byte7 (
    .READWRITE(not_1_out), .ADDR(and_7_out), .CLK(CLK), .bit1(byte7_bit1[0]), .bit2(byte7_bit1[1]),
    .bit3(byte7_bit1[2]), .bit4(byte7_bit1[3]), .input1(DATA_IN[0]), .input2(DATA_IN[1]),
    .input3(DATA_IN[2]), .input4(DATA_IN[3]), .bit5(byte7_bit1[4]), .bit6(byte7_bit1[5]),
    .bit7(byte7_bit1[6]), .bit8(byte7_bit1[7]), .input6(DATA_IN[5]), .input7(DATA_IN[6]),
    .input8(DATA_IN[7]), .input5(DATA_IN[4]), .ROMON(multiplexer_18_out), .RAMOUT(multiplexer_17_out));  // open: out_14, out_15, out_16, out_17, out_18, out_19, out_20, out_21
  ram byte8 (
    .READWRITE(not_1_out), .ADDR(and_8_out), .CLK(CLK), .bit1(byte8_bit1[0]), .bit2(byte8_bit1[1]),
    .bit3(byte8_bit1[2]), .bit4(byte8_bit1[3]), .input1(DATA_IN[0]), .input2(DATA_IN[1]),
    .input3(DATA_IN[2]), .input4(DATA_IN[3]), .bit5(byte8_bit1[4]), .bit6(byte8_bit1[5]),
    .bit7(byte8_bit1[6]), .bit8(byte8_bit1[7]), .input6(DATA_IN[5]), .input7(DATA_IN[6]),
    .input8(DATA_IN[7]), .input5(DATA_IN[4]), .ROMON(multiplexer_20_out), .RAMOUT(multiplexer_19_out));  // open: out_14, out_15, out_16, out_17, out_18, out_19, out_20, out_21
  ram byte9 (
    .READWRITE(not_1_out), .ADDR(and_9_out), .CLK(CLK), .bit1(byte9_bit1[0]), .bit2(byte9_bit1[1]),
    .bit3(byte9_bit1[2]), .bit4(byte9_bit1[3]), .input1(DATA_IN[0]), .input2(DATA_IN[1]),
    .input3(DATA_IN[2]), .input4(DATA_IN[3]), .bit5(byte9_bit1[4]), .bit6(byte9_bit1[5]),
    .bit7(byte9_bit1[6]), .bit8(byte9_bit1[7]), .input6(DATA_IN[5]), .input7(DATA_IN[6]),
    .input8(DATA_IN[7]), .input5(DATA_IN[4]), .ROMON(multiplexer_22_out), .RAMOUT(multiplexer_21_out));  // open: out_14, out_15, out_16, out_17, out_18, out_19, out_20, out_21
  ram byte10 (
    .READWRITE(not_1_out), .ADDR(and_10_out), .CLK(CLK), .bit1(byte10_bit1[0]), .bit2(byte10_bit1[1]),
    .bit3(byte10_bit1[2]), .bit4(byte10_bit1[3]), .input1(DATA_IN[0]), .input2(DATA_IN[1]),
    .input3(DATA_IN[2]), .input4(DATA_IN[3]), .bit5(byte10_bit1[4]), .bit6(byte10_bit1[5]),
    .bit7(byte10_bit1[6]), .bit8(byte10_bit1[7]), .input6(DATA_IN[5]), .input7(DATA_IN[6]),
    .input8(DATA_IN[7]), .input5(DATA_IN[4]), .ROMON(multiplexer_24_out), .RAMOUT(multiplexer_23_out));  // open: out_14, out_15, out_16, out_17, out_18, out_19, out_20, out_21
  ram byte11 (
    .READWRITE(not_1_out), .ADDR(and_11_out), .CLK(CLK), .bit1(byte11_bit1[0]), .bit2(byte11_bit1[1]),
    .bit3(byte11_bit1[2]), .bit4(byte11_bit1[3]), .input1(DATA_IN[0]), .input2(DATA_IN[1]),
    .input3(DATA_IN[2]), .input4(DATA_IN[3]), .bit5(byte11_bit1[4]), .bit6(byte11_bit1[5]),
    .bit7(byte11_bit1[6]), .bit8(byte11_bit1[7]), .input6(DATA_IN[5]), .input7(DATA_IN[6]),
    .input8(DATA_IN[7]), .input5(DATA_IN[4]), .ROMON(multiplexer_26_out), .RAMOUT(multiplexer_25_out));  // open: out_14, out_15, out_16, out_17, out_18, out_19, out_20, out_21
  ram byte12 (
    .READWRITE(not_1_out), .ADDR(and_12_out), .CLK(CLK), .bit1(byte12_bit1[0]), .bit2(byte12_bit1[1]),
    .bit3(byte12_bit1[2]), .bit4(byte12_bit1[3]), .input1(DATA_IN[0]), .input2(DATA_IN[1]),
    .input3(DATA_IN[2]), .input4(DATA_IN[3]), .bit5(byte12_bit1[4]), .bit6(byte12_bit1[5]),
    .bit7(byte12_bit1[6]), .bit8(byte12_bit1[7]), .input6(DATA_IN[5]), .input7(DATA_IN[6]),
    .input8(DATA_IN[7]), .input5(DATA_IN[4]), .ROMON(multiplexer_28_out), .RAMOUT(multiplexer_27_out));  // open: out_14, out_15, out_16, out_17, out_18, out_19, out_20, out_21
  ram byte13 (
    .READWRITE(not_1_out), .ADDR(and_13_out), .CLK(CLK), .bit1(byte13_bit1[0]), .bit2(byte13_bit1[1]),
    .bit3(byte13_bit1[2]), .bit4(byte13_bit1[3]), .input1(DATA_IN[0]), .input2(DATA_IN[1]),
    .input3(DATA_IN[2]), .input4(DATA_IN[3]), .bit5(byte13_bit1[4]), .bit6(byte13_bit1[5]),
    .bit7(byte13_bit1[6]), .bit8(byte13_bit1[7]), .input6(DATA_IN[5]), .input7(DATA_IN[6]),
    .input8(DATA_IN[7]), .input5(DATA_IN[4]), .ROMON(multiplexer_30_out), .RAMOUT(multiplexer_29_out));  // open: out_14, out_15, out_16, out_17, out_18, out_19, out_20, out_21
  ram byte14 (
    .READWRITE(not_1_out), .ADDR(and_14_out), .CLK(CLK), .bit1(byte14_bit1[0]), .bit2(byte14_bit1[1]),
    .bit3(byte14_bit1[2]), .bit4(byte14_bit1[3]), .input1(DATA_IN[0]), .input2(DATA_IN[1]),
    .input3(DATA_IN[2]), .input4(DATA_IN[3]), .bit5(byte14_bit1[4]), .bit6(byte14_bit1[5]),
    .bit7(byte14_bit1[6]), .bit8(byte14_bit1[7]), .input6(DATA_IN[5]), .input7(DATA_IN[6]),
    .input8(DATA_IN[7]), .input5(DATA_IN[4]), .ROMON(multiplexer_32_out), .RAMOUT(multiplexer_31_out));  // open: out_14, out_15, out_16, out_17, out_18, out_19, out_20, out_21
  ram byte15 (
    .READWRITE(not_1_out), .ADDR(and_15_out), .CLK(CLK), .bit1(byte15_bit1[0]), .bit2(byte15_bit1[1]),
    .bit3(byte15_bit1[2]), .bit4(byte15_bit1[3]), .input1(DATA_IN[0]), .input2(DATA_IN[1]),
    .input3(DATA_IN[2]), .input4(DATA_IN[3]), .bit5(byte15_bit1[4]), .bit6(byte15_bit1[5]),
    .bit7(byte15_bit1[6]), .bit8(byte15_bit1[7]), .input6(DATA_IN[5]), .input7(DATA_IN[6]),
    .input8(DATA_IN[7]), .input5(DATA_IN[4]), .ROMON(multiplexer_34_out), .RAMOUT(multiplexer_33_out));  // open: out_14, out_15, out_16, out_17, out_18, out_19, out_20, out_21
  ram byte16 (
    .READWRITE(not_1_out), .ADDR(and_16_out), .CLK(CLK), .bit1(byte16_bit1[0]), .bit2(byte16_bit1[1]),
    .bit3(byte16_bit1[2]), .bit4(byte16_bit1[3]), .input1(DATA_IN[0]), .input2(DATA_IN[1]),
    .input3(DATA_IN[2]), .input4(DATA_IN[3]), .bit5(byte16_bit1[4]), .bit6(byte16_bit1[5]),
    .bit7(byte16_bit1[6]), .bit8(byte16_bit1[7]), .input6(DATA_IN[5]), .input7(DATA_IN[6]),
    .input8(DATA_IN[7]), .input5(DATA_IN[4]), .ROMON(or_4_out), .RAMOUT(multiplexer_36_out));  // open: out_14, out_15, out_16, out_17, out_18, out_19, out_20, out_21
  assign or_1_out = multiplexer_1_out | multiplexer_3_out;  // OR_Gate or_1, 8 bits wide
  assign or_2_out = multiplexer_4_out | multiplexer_6_out;  // OR_Gate or_2, 8 bits wide
  assign or_3_out = multiplexer_7_out | multiplexer_9_out;  // OR_Gate or_3, 8 bits wide
  assign or_4_out = multiplexer_35_out | multiplexer_37_out;  // OR_Gate or_4, 8 bits wide
  Multiplexer #(.width(8), .enable("false")) multiplexer_1 (
    .in0({8{1'b0}}), .in1(8'h1f), .out(multiplexer_1_out), .sel(multiply_rom));
  Multiplexer #(.width(8), .enable("false")) multiplexer_2 (
    .in0({8{1'b0}}), .in1({8{1'b1}}), .out(multiplexer_2_out), .sel(on_off_switch));
  Multiplexer #(.width(8), .enable("false")) multiplexer_3 (
    .in0({8{1'b0}}), .in1(8'h90), .out(multiplexer_3_out), .sel(program_rom));
  Multiplexer #(.width(8), .enable("false")) multiplexer_4 (
    .in0({8{1'b0}}), .in1({4'b1111, mul1_constant}), .out(multiplexer_4_out), .sel(multiply_rom));
  Multiplexer #(.width(8), .enable("false")) multiplexer_5 (
    .in0({8{1'b0}}), .in1({8{1'b1}}), .out(multiplexer_5_out), .sel(on_off_switch));
  Multiplexer #(.width(8), .enable("false")) multiplexer_6 (
    .in0({8{1'b0}}), .in1(8'h1a), .out(multiplexer_6_out), .sel(program_rom));
  Multiplexer #(.width(8), .enable("false")) multiplexer_7 (
    .in0({8{1'b0}}), .in1(8'hc0), .out(multiplexer_7_out), .sel(multiply_rom));
  Multiplexer #(.width(8), .enable("false")) multiplexer_8 (
    .in0({8{1'b0}}), .in1({8{1'b1}}), .out(multiplexer_8_out), .sel(on_off_switch));
  Multiplexer #(.width(8), .enable("false")) multiplexer_9 (
    .in0({8{1'b0}}), .in1(8'h40), .out(multiplexer_9_out), .sel(program_rom));
  assign RAM_OUT = byte1_bit1 | byte2_bit1 | byte3_bit1 | byte4_bit1 | byte5_bit1 | byte6_bit1 | byte7_bit1 | byte8_bit1 | byte9_bit1 | byte10_bit1 | byte11_bit1 | byte12_bit1 | byte13_bit1 | byte14_bit1 | byte15_bit1 | byte16_bit1;  // OR_Gate or_5, 8 bits wide
  Multiplexer #(.width(8), .enable("false")) multiplexer_10 (
    .in0({8{1'b0}}), .in1({8{1'b1}}), .out(multiplexer_10_out), .sel(on_off_switch));
  Multiplexer #(.width(8), .enable("false")) multiplexer_11 (
    .in0({8{1'b0}}), .in1(8'h2a), .out(multiplexer_11_out), .sel(program_rom));
  assign or_6_out = multiplexer_11_out | multiplexer_12_out;  // OR_Gate or_6, 8 bits wide
  Multiplexer #(.width(8), .enable("false")) multiplexer_12 (
    .in0({8{1'b0}}), .in1(8'hd0), .out(multiplexer_12_out), .sel(multiply_rom));
  Multiplexer #(.width(8), .enable("false")) multiplexer_13 (
    .in0({8{1'b0}}), .in1({8{1'b1}}), .out(multiplexer_13_out), .sel(on_off_switch));
  Multiplexer #(.width(8), .enable("false")) multiplexer_14 (
    .in0({8{1'b0}}), .in1(8'h8), .out(multiplexer_14_out), .sel(program_rom));
  Multiplexer #(.width(8), .enable("false")) multiplexer_15 (
    .in0({8{1'b0}}), .in1({8{1'b1}}), .out(multiplexer_15_out), .sel(on_off_switch));
  Multiplexer #(.width(8), .enable("false")) multiplexer_16 (
    .in0({8{1'b0}}), .in1(8'h19), .out(multiplexer_16_out), .sel(program_rom));
  Multiplexer #(.width(8), .enable("false")) multiplexer_17 (
    .in0({8{1'b0}}), .in1({8{1'b1}}), .out(multiplexer_17_out), .sel(on_off_switch));
  Multiplexer #(.width(8), .enable("false")) multiplexer_18 (
    .in0({8{1'b0}}), .in1(8'h7b), .out(multiplexer_18_out), .sel(program_rom));
  Multiplexer #(.width(8), .enable("false")) multiplexer_19 (
    .in0({8{1'b0}}), .in1({8{1'b1}}), .out(multiplexer_19_out), .sel(on_off_switch));
  Multiplexer #(.width(8), .enable("false")) multiplexer_20 (
    .in0({8{1'b0}}), .in1(8'h8e), .out(multiplexer_20_out), .sel(program_rom));
  Multiplexer #(.width(8), .enable("false")) multiplexer_21 (
    .in0({8{1'b0}}), .in1({8{1'b1}}), .out(multiplexer_21_out), .sel(on_off_switch));
  Multiplexer #(.width(8), .enable("false")) multiplexer_22 (
    .in0({8{1'b0}}), .in1(8'h1), .out(multiplexer_22_out), .sel(program_rom));
  Multiplexer #(.width(8), .enable("false")) multiplexer_23 (
    .in0({8{1'b0}}), .in1({8{1'b1}}), .out(multiplexer_23_out), .sel(on_off_switch));
  Multiplexer #(.width(8), .enable("false")) multiplexer_24 (
    .in0({8{1'b0}}), .in1(8'h4), .out(multiplexer_24_out), .sel(program_rom));
  Multiplexer #(.width(8), .enable("false")) multiplexer_25 (
    .in0({8{1'b0}}), .in1({8{1'b1}}), .out(multiplexer_25_out), .sel(on_off_switch));
  Multiplexer #(.width(8), .enable("false")) multiplexer_26 (
    .in0({8{1'b0}}), .in1({8{1'b0}}), .out(multiplexer_26_out), .sel(program_rom));
  Multiplexer #(.width(8), .enable("false")) multiplexer_27 (
    .in0({8{1'b0}}), .in1({8{1'b1}}), .out(multiplexer_27_out), .sel(on_off_switch));
  Multiplexer #(.width(8), .enable("false")) multiplexer_28 (
    .in0({8{1'b0}}), .in1(8'ha), .out(multiplexer_28_out), .sel(program_rom));
  Multiplexer #(.width(8), .enable("false")) multiplexer_29 (
    .in0({8{1'b0}}), .in1({8{1'b1}}), .out(multiplexer_29_out), .sel(on_off_switch));
  Multiplexer #(.width(8), .enable("false")) multiplexer_30 (
    .in0({8{1'b0}}), .in1(8'hb0), .out(multiplexer_30_out), .sel(program_rom));
  Multiplexer #(.width(8), .enable("false")) multiplexer_31 (
    .in0({8{1'b0}}), .in1({8{1'b1}}), .out(multiplexer_31_out), .sel(on_off_switch));
  Multiplexer #(.width(8), .enable("false")) multiplexer_32 (
    .in0({8{1'b0}}), .in1(8'hd0), .out(multiplexer_32_out), .sel(program_rom));
  Multiplexer #(.width(8), .enable("false")) multiplexer_33 (
    .in0({8{1'b0}}), .in1({8{1'b1}}), .out(multiplexer_33_out), .sel(on_off_switch));
  Multiplexer #(.width(8), .enable("false")) multiplexer_34 (
    .in0({8{1'b0}}), .in1(8'h60), .out(multiplexer_34_out), .sel(program_rom));
  Multiplexer #(.width(8), .enable("false")) multiplexer_35 (
    .in0({8{1'b0}}), .in1(mul2), .out(multiplexer_35_out), .sel(multiply_rom));
  Multiplexer #(.width(8), .enable("false")) multiplexer_36 (
    .in0({8{1'b0}}), .in1({8{1'b1}}), .out(multiplexer_36_out), .sel(on_off_switch));
  Multiplexer #(.width(8), .enable("false")) multiplexer_37 (
    .in0({8{1'b0}}), .in1(8'h39), .out(multiplexer_37_out), .sel(program_rom));
endmodule

module DR (
  input  [7:0] IN,
  input  readwrite,
  input  clk,
  input  on_off_switch,
  output [7:0] out_5,
  output [7:0] DATA_OUT
);

  wire and_1_out, and_2_out, and_3_out, and_4_out, and_5_out, and_6_out, and_7_out, and_8_out, and_9_out,
       and_10_out, and_11_out, and_12_out, and_13_out, and_14_out, and_15_out, and_16_out, multiplexer_1_out,
       multiplexer_2_out, multiplexer_3_out, multiplexer_4_out, multiplexer_5_out, multiplexer_6_out,
       multiplexer_7_out, multiplexer_8_out, not_1_out, not_2_out, not_3_out, not_4_out, not_5_out,
       not_6_out, not_7_out, not_8_out, not_9_out, not_10_out;

  not not_1 (not_1_out, readwrite);
  not not_2 (not_2_out, IN[0]);
  not not_3 (not_3_out, IN[1]);
  not not_4 (not_4_out, IN[2]);
  not not_5 (not_5_out, IN[3]);
  not not_6 (not_6_out, IN[4]);
  not not_7 (not_7_out, IN[5]);
  not not_8 (not_8_out, IN[6]);
  not not_9 (not_9_out, not_1_out);
  not not_10 (not_10_out, IN[7]);
  and and_1 (and_1_out, not_9_out, IN[0]);
  S_R_Flip_Flop s_r_ff_1 (
    .S(and_1_out), .R(and_2_out), .clk(clk), .Q(out_5[0]), .reset(multiplexer_4_out));  // open: Qn, preset
  and and_2 (and_2_out, not_9_out, not_2_out);
  and and_3 (and_3_out, not_9_out, IN[1]);
  S_R_Flip_Flop s_r_ff_2 (
    .S(and_3_out), .R(and_4_out), .clk(clk), .Q(out_5[1]), .reset(multiplexer_5_out));  // open: Qn, preset
  and and_4 (and_4_out, not_9_out, not_3_out);
  S_R_Flip_Flop s_r_ff_3 (
    .S(and_5_out), .R(and_6_out), .clk(clk), .Q(out_5[2]), .reset(multiplexer_6_out));  // open: Qn, preset
  and and_5 (and_5_out, not_9_out, IN[2]);
  and and_6 (and_6_out, not_9_out, not_4_out);
  and and_7 (and_7_out, not_9_out, IN[3]);
  S_R_Flip_Flop s_r_ff_4 (
    .S(and_7_out), .R(and_8_out), .clk(clk), .Q(out_5[3]), .reset(multiplexer_7_out));  // open: Qn, preset
  and and_8 (and_8_out, not_9_out, not_5_out);
  and and_9 (and_9_out, not_9_out, IN[4]);
  S_R_Flip_Flop s_r_ff_5 (
    .S(and_9_out), .R(and_10_out), .clk(clk), .Q(out_5[4]), .reset(multiplexer_8_out));  // open: Qn, preset
  and and_10 (and_10_out, not_9_out, not_6_out);
  S_R_Flip_Flop s_r_ff_6 (
    .S(and_11_out), .R(and_12_out), .clk(clk), .Q(out_5[5]), .reset(multiplexer_1_out));  // open: Qn, preset
  and and_11 (and_11_out, not_9_out, IN[5]);
  and and_12 (and_12_out, not_9_out, not_7_out);
  S_R_Flip_Flop s_r_ff_7 (
    .S(and_13_out), .R(and_14_out), .clk(clk), .Q(out_5[6]), .reset(multiplexer_2_out));  // open: Qn, preset
  and and_13 (and_13_out, not_9_out, IN[6]);
  and and_14 (and_14_out, not_9_out, not_8_out);
  S_R_Flip_Flop s_r_ff_8 (
    .S(and_15_out), .R(and_16_out), .clk(clk), .Q(out_5[7]), .reset(multiplexer_3_out));  // open: Qn, preset
  and and_15 (and_15_out, not_9_out, IN[7]);
  and and_16 (and_16_out, not_9_out, not_10_out);
  and and_17 (DATA_OUT[3], out_5[3], not_1_out);
  and and_18 (DATA_OUT[4], out_5[4], not_1_out);
  and and_19 (DATA_OUT[5], out_5[5], not_1_out);
  and and_20 (DATA_OUT[6], out_5[6], not_1_out);
  and and_21 (DATA_OUT[7], out_5[7], not_1_out);
  and and_22 (DATA_OUT[0], out_5[0], not_1_out);
  and and_23 (DATA_OUT[1], out_5[1], not_1_out);
  and and_24 (DATA_OUT[2], out_5[2], not_1_out);
  Multiplexer #(.enable("false")) multiplexer_1 (.in0(1'b0), .in1(1'b1), .out(multiplexer_1_out), .sel(on_off_switch));
  Multiplexer #(.enable("false")) multiplexer_2 (.in0(1'b0), .in1(1'b1), .out(multiplexer_2_out), .sel(on_off_switch));
  Multiplexer #(.enable("false")) multiplexer_3 (.in0(1'b0), .in1(1'b1), .out(multiplexer_3_out), .sel(on_off_switch));
  Multiplexer #(.enable("false")) multiplexer_4 (.in0(1'b0), .in1(1'b1), .out(multiplexer_4_out), .sel(on_off_switch));
  Multiplexer #(.enable("false")) multiplexer_5 (.in0(1'b0), .in1(1'b1), .out(multiplexer_5_out), .sel(on_off_switch));
  Multiplexer #(.enable("false")) multiplexer_6 (.in0(1'b0), .in1(1'b1), .out(multiplexer_6_out), .sel(on_off_switch));
  Multiplexer #(.enable("false")) multiplexer_7 (.in0(1'b0), .in1(1'b1), .out(multiplexer_7_out), .sel(on_off_switch));
  Multiplexer #(.enable("false")) multiplexer_8 (.in0(1'b0), .in1(1'b1), .out(multiplexer_8_out), .sel(on_off_switch));
  Multiplexer #(.enable("false")) multiplexer_9 (.in0(1'b0), .in1(1'b1), .sel(on_off_switch));  // open: out

  // Notes on the sheet:
  //   Data register
endmodule

module MAR_6e5ae79d (
  input  [3:0] PC_IN,
  input  CU_CONTROL,
  input  CLK,
  output [3:0] out_4,
  output [3:0] ADDR_OUT
);

  wire and_1_out, and_2_out, and_3_out, and_4_out, and_5_out, and_6_out, and_7_out, and_8_out, not_1_out,
       not_2_out, not_3_out, not_4_out;

  and and_1 (and_1_out, CU_CONTROL, PC_IN[0]);
  and and_2 (and_2_out, CU_CONTROL, not_1_out);
  not not_1 (not_1_out, PC_IN[0]);
  and and_3 (and_3_out, CU_CONTROL, PC_IN[1]);
  and and_4 (and_4_out, CU_CONTROL, not_2_out);
  not not_2 (not_2_out, PC_IN[1]);
  and and_5 (and_5_out, CU_CONTROL, PC_IN[2]);
  and and_6 (and_6_out, CU_CONTROL, not_3_out);
  not not_3 (not_3_out, PC_IN[2]);
  and and_7 (and_7_out, CU_CONTROL, PC_IN[3]);
  and and_8 (and_8_out, CU_CONTROL, not_4_out);
  not not_4 (not_4_out, PC_IN[3]);
  S_R_Flip_Flop s_r_ff_1 (.S(and_1_out), .R(and_2_out), .clk(CLK), .Q(ADDR_OUT[0]));  // open: reset, Qn, preset
  S_R_Flip_Flop s_r_ff_2 (.S(and_3_out), .R(and_4_out), .clk(CLK), .Q(ADDR_OUT[1]));  // open: reset, Qn, preset
  S_R_Flip_Flop s_r_ff_3 (.S(and_5_out), .R(and_6_out), .clk(CLK), .Q(ADDR_OUT[2]));  // open: reset, Qn, preset
  S_R_Flip_Flop s_r_ff_4 (.S(and_7_out), .R(and_8_out), .clk(CLK), .Q(ADDR_OUT[3]));  // open: reset, Qn, preset

  assign out_4 = ADDR_OUT;
endmodule

module MODE (
  input  CU_IN,
  input  CU_CONTROL,
  input  CLK,
  output out_4,
  output MODE_OUT
);

  wire and_1_out, and_2_out, not_1_out, not_2_out;

  not not_1 (not_1_out, CU_IN);
  not not_2 (not_2_out, CU_CONTROL);
  and and_1 (and_1_out, not_2_out, CU_IN);
  S_R_Flip_Flop s_r_ff_1 (.S(and_1_out), .R(and_2_out), .clk(CLK), .Q(out_4));  // open: reset, Qn, preset
  and and_2 (and_2_out, not_2_out, not_1_out);
  and and_3 (MODE_OUT, out_4, CU_CONTROL);
endmodule

module ram (
  input  [7:0] ROMON,
  input  ADDR,
  input  READWRITE,
  input  input1,
  input  input2,
  input  [7:0] RAMOUT,
  input  input3,
  input  input4,
  input  input5,
  input  input6,
  input  input7,
  input  input8,
  input  CLK,
  output out_14,
  output out_15,
  output out_16,
  output out_17,
  output out_18,
  output out_19,
  output out_20,
  output out_21,
  output bit1,
  output bit2,
  output bit3,
  output bit4,
  output bit5,
  output bit6,
  output bit7,
  output bit8
);

  wire and_1_out, and_2_out, and_3_out, and_4_out, and_5_out, and_6_out, and_7_out, and_8_out, and_9_out,
       and_10_out, and_11_out, and_12_out, and_13_out, and_14_out, and_15_out, and_16_out, not_1_out,
       not_2_out, not_3_out, not_4_out, not_5_out, not_6_out, not_7_out, not_8_out, not_9_out;

  not not_1 (not_1_out, READWRITE);
  not not_2 (not_2_out, input1);
  not not_3 (not_3_out, input2);
  not not_4 (not_4_out, input3);
  not not_5 (not_5_out, input4);
  not not_6 (not_6_out, input5);
  not not_7 (not_7_out, input6);
  not not_8 (not_8_out, input7);
  not not_9 (not_9_out, input8);
  and and_1 (and_1_out, not_1_out, ADDR, input1);
  and and_2 (and_2_out, not_1_out, ADDR, not_2_out);
  and and_3 (and_3_out, not_1_out, ADDR, input2);
  and and_4 (and_4_out, not_1_out, ADDR, not_3_out);
  and and_5 (and_5_out, not_1_out, ADDR, input3);
  and and_6 (and_6_out, not_1_out, ADDR, not_4_out);
  and and_7 (and_7_out, not_1_out, ADDR, input4);
  and and_8 (and_8_out, not_1_out, ADDR, not_5_out);
  and and_9 (and_9_out, not_1_out, ADDR, input5);
  and and_10 (and_10_out, not_1_out, ADDR, not_6_out);
  and and_11 (and_11_out, not_1_out, ADDR, input6);
  and and_12 (and_12_out, not_1_out, ADDR, not_7_out);
  and and_13 (and_13_out, not_1_out, ADDR, input7);
  and and_14 (and_14_out, not_1_out, ADDR, not_8_out);
  and and_15 (and_15_out, not_1_out, ADDR, input8);
  and and_16 (and_16_out, not_1_out, ADDR, not_9_out);
  S_R_Flip_Flop s_r_ff_1 (
    .S(and_1_out), .R(and_2_out), .clk(CLK), .Q(out_14), .reset(RAMOUT[0]), .preset(ROMON[0]));  // open: Qn
  S_R_Flip_Flop s_r_ff_2 (
    .S(and_3_out), .R(and_4_out), .clk(CLK), .Q(out_15), .reset(RAMOUT[1]), .preset(ROMON[1]));  // open: Qn
  S_R_Flip_Flop s_r_ff_3 (
    .S(and_5_out), .R(and_6_out), .clk(CLK), .Q(out_16), .reset(RAMOUT[2]), .preset(ROMON[2]));  // open: Qn
  S_R_Flip_Flop s_r_ff_4 (
    .S(and_7_out), .R(and_8_out), .clk(CLK), .Q(out_17), .reset(RAMOUT[3]), .preset(ROMON[3]));  // open: Qn
  S_R_Flip_Flop s_r_ff_5 (
    .S(and_9_out), .R(and_10_out), .clk(CLK), .Q(out_18), .reset(RAMOUT[4]), .preset(ROMON[4]));  // open: Qn
  S_R_Flip_Flop s_r_ff_6 (
    .S(and_11_out), .R(and_12_out), .clk(CLK), .Q(out_19), .reset(RAMOUT[5]), .preset(ROMON[5]));  // open: Qn
  S_R_Flip_Flop s_r_ff_7 (
    .S(and_13_out), .R(and_14_out), .clk(CLK), .Q(out_20), .reset(RAMOUT[6]), .preset(ROMON[6]));  // open: Qn
  S_R_Flip_Flop s_r_ff_8 (
    .S(and_15_out), .R(and_16_out), .clk(CLK), .Q(out_21), .reset(RAMOUT[7]), .preset(ROMON[7]));  // open: Qn
  and and_17 (bit1, out_14, READWRITE, ADDR);
  and and_18 (bit2, out_15, READWRITE, ADDR);
  and and_19 (bit3, out_16, READWRITE, ADDR);
  and and_20 (bit4, out_17, READWRITE, ADDR);
  and and_21 (bit5, out_18, READWRITE, ADDR);
  and and_22 (bit6, out_19, READWRITE, ADDR);
  and and_23 (bit7, out_20, READWRITE, ADDR);
  and and_24 (bit8, out_21, READWRITE, ADDR);
endmodule

module ALU_43ff114b (
  input  Add1SUB0,
  input  [7:0] L,
  input  [7:0] R,
  output [2:0] out_4,
  output [7:0] OUTPUT
);

  wire fadder_1_cout, fadder_2_cout, fadder_3_cout, fadder_4_cout, fadder_5_cout, fadder_6_cout,
       fadder_7_cout, not_1_out, not_2_out, not_3_out, not_4_out, not_5_out, not_6_out, not_7_out, not_8_out,
       not_9_out, xnor_1_out, xor_1_out, xor_2_out, xor_3_out, xor_4_out, xor_5_out, xor_6_out, xor_7_out,
       xor_8_out, xor_9_out;

  Fadder fadder_1 (.Cin(not_1_out), .A(R[0]), .B(xor_1_out), .Sum(OUTPUT[0]), .Cout(fadder_1_cout));
  xor xor_1 (xor_1_out, L[0], not_1_out);
  Fadder fadder_2 (.Cin(fadder_1_cout), .A(R[1]), .B(xor_2_out), .Sum(OUTPUT[1]), .Cout(fadder_2_cout));
  xor xor_2 (xor_2_out, L[1], not_1_out);
  Fadder fadder_3 (.Cin(fadder_2_cout), .A(R[2]), .B(xor_3_out), .Sum(OUTPUT[2]), .Cout(fadder_3_cout));
  xor xor_3 (xor_3_out, L[2], not_1_out);
  Fadder fadder_4 (.Cin(fadder_3_cout), .A(R[3]), .B(xor_4_out), .Sum(OUTPUT[3]), .Cout(fadder_4_cout));
  xor xor_4 (xor_4_out, L[3], not_1_out);
  Fadder fadder_5 (.Cin(fadder_4_cout), .A(R[4]), .B(xor_5_out), .Sum(OUTPUT[4]), .Cout(fadder_5_cout));
  xor xor_5 (xor_5_out, L[4], not_1_out);
  Fadder fadder_6 (.Cin(fadder_5_cout), .A(R[5]), .B(xor_6_out), .Sum(OUTPUT[5]), .Cout(fadder_6_cout));
  xor xor_6 (xor_6_out, L[5], not_1_out);
  Fadder fadder_7 (.Cin(fadder_6_cout), .A(R[7]), .B(xor_7_out), .Sum(OUTPUT[6]), .Cout(fadder_7_cout));
  xor xor_7 (xor_7_out, L[6], not_1_out);
  Fadder fadder_8 (.Cin(fadder_7_cout), .A(R[6]), .B(xor_8_out), .Sum(out_4[1]));  // open: Cout
  xor xor_8 (xor_8_out, L[7], not_1_out);
  not not_1 (not_1_out, Add1SUB0);
  xnor xnor_1 (xnor_1_out, xor_8_out, L[7]);
  not not_2 (not_2_out, OUTPUT[0]);
  not not_3 (not_3_out, OUTPUT[1]);
  not not_4 (not_4_out, OUTPUT[2]);
  not not_5 (not_5_out, OUTPUT[3]);
  not not_6 (not_6_out, OUTPUT[4]);
  not not_7 (not_7_out, OUTPUT[5]);
  not not_8 (not_8_out, OUTPUT[6]);
  not not_9 (not_9_out, out_4[1]);
  and and_1 (out_4[0], not_2_out, not_3_out, not_4_out, not_5_out, not_6_out, not_7_out, not_8_out, not_9_out);
  xor xor_9 (xor_9_out, out_4[1], xor_8_out);
  and and_2 (out_4[2], xor_9_out, xnor_1_out);

  assign OUTPUT[7] = out_4[1];
endmodule

module Fadder (
  input  Cin,
  input  A,
  input  B,
  output Sum,
  output Cout
);

  wire and_1_out, and_2_out, xor_1_out;

  xor xor_1 (xor_1_out, Cin, A);
  and and_1 (and_1_out, Cin, A);
  xor xor_2 (Sum, xor_1_out, B);
  and and_2 (and_2_out, xor_1_out, B);
  or or_1 (Cout, and_1_out, and_2_out);
endmodule

module Status (
  input  [2:0] in_1,
  input  CLK,
  input  ReadWrite,
  output out_4,
  output zero,
  output negative,
  output overflow
);

  wire and_1_out, and_2_out, and_3_out, and_4_out, and_5_out, and_6_out, not_1_out, not_2_out, not_3_out,
       not_4_out, s_r_ff_2_q, s_r_ff_3_q;

  and and_1 (and_1_out, ReadWrite, in_1[0]);
  and and_2 (and_2_out, ReadWrite, not_1_out);
  not not_1 (not_1_out, in_1[0]);
  and and_3 (and_3_out, ReadWrite, in_1[1]);
  and and_4 (and_4_out, ReadWrite, not_2_out);
  not not_2 (not_2_out, in_1[1]);
  and and_5 (and_5_out, ReadWrite, in_1[2]);
  and and_6 (and_6_out, ReadWrite, not_3_out);
  not not_3 (not_3_out, in_1[2]);
  not not_4 (not_4_out, ReadWrite);
  S_R_Flip_Flop s_r_ff_1 (.S(and_1_out), .R(and_2_out), .clk(CLK), .Q(out_4));  // open: reset, Qn, preset
  S_R_Flip_Flop s_r_ff_2 (.S(and_3_out), .R(and_4_out), .clk(CLK), .Q(s_r_ff_2_q));  // open: reset, Qn, preset
  S_R_Flip_Flop s_r_ff_3 (.S(and_5_out), .R(and_6_out), .clk(CLK), .Q(s_r_ff_3_q));  // open: reset, Qn, preset
  and and_7 (zero, out_4, not_4_out);
  and and_8 (negative, s_r_ff_2_q, not_4_out);
  and and_9 (overflow, s_r_ff_3_q, not_4_out);

  // Notes on the sheet:
  //   zero
  //   overflow
  //   negative
endmodule

module INC (
  input  [3:0] A,
  input  in_2,
  output [3:0] R
);

  wire fadder_1_cout, fadder_2_cout, fadder_3_cout, multiplexer_1_out, not_1_out, xor_1_out, xor_2_out,
       xor_3_out, xor_4_out;

  // Probe on A
  Multiplexer #(.enable("false")) multiplexer_1 (.in0(1'b1), .in1(1'b0), .out(multiplexer_1_out), .sel(in_2));
  Fadder fadder_1 (.Cin(not_1_out), .A(A[0]), .B(xor_1_out), .Sum(R[0]), .Cout(fadder_1_cout));
  xor xor_1 (xor_1_out, 1'b1, not_1_out);
  Fadder fadder_2 (.Cin(fadder_1_cout), .A(A[1]), .B(xor_2_out), .Sum(R[1]), .Cout(fadder_2_cout));
  xor xor_2 (xor_2_out, 1'b0, not_1_out);
  Fadder fadder_3 (.Cin(fadder_2_cout), .A(A[2]), .B(xor_3_out), .Sum(R[2]), .Cout(fadder_3_cout));
  xor xor_3 (xor_3_out, 1'b0, not_1_out);
  Fadder fadder_4 (.Cin(fadder_3_cout), .A(A[3]), .B(xor_4_out), .Sum(R[3]));  // open: Cout
  xor xor_4 (xor_4_out, 1'b0, not_1_out);
  not not_1 (not_1_out, multiplexer_1_out);
  // Probe on R
endmodule

module Count (
  input  [3:0] IN,
  input  CLK,
  output [3:0] OUT
);

  wire not_1_out, not_2_out, not_3_out, not_4_out;

  not not_1 (not_1_out, IN[0]);
  not not_2 (not_2_out, IN[1]);
  not not_3 (not_3_out, IN[2]);
  not not_4 (not_4_out, IN[3]);
  S_R_Flip_Flop s_r_ff_1 (.S(IN[0]), .R(not_1_out), .clk(CLK), .Q(OUT[0]));  // open: reset, Qn, preset
  S_R_Flip_Flop s_r_ff_2 (.S(IN[1]), .R(not_2_out), .clk(CLK), .Q(OUT[1]));  // open: reset, Qn, preset
  S_R_Flip_Flop s_r_ff_3 (.S(IN[2]), .R(not_3_out), .clk(CLK), .Q(OUT[2]));  // open: reset, Qn, preset
  S_R_Flip_Flop s_r_ff_4 (.S(IN[3]), .R(not_4_out), .clk(CLK), .Q(OUT[3]));  // open: reset, Qn, preset
endmodule

module AR (
  input  [3:0] PC_IN,
  input  CU_CONTROL,
  input  CLK,
  output [3:0] out_4,
  output [3:0] ADDR_OUT
);

  wire and_1_out, and_2_out, and_3_out, and_4_out, and_5_out, and_6_out, and_7_out, and_8_out, not_1_out,
       not_2_out, not_3_out, not_4_out;

  and and_1 (and_1_out, CU_CONTROL, PC_IN[0]);
  and and_2 (and_2_out, CU_CONTROL, not_1_out);
  not not_1 (not_1_out, PC_IN[0]);
  and and_3 (and_3_out, CU_CONTROL, PC_IN[1]);
  and and_4 (and_4_out, CU_CONTROL, not_2_out);
  not not_2 (not_2_out, PC_IN[1]);
  and and_5 (and_5_out, CU_CONTROL, PC_IN[2]);
  and and_6 (and_6_out, CU_CONTROL, not_3_out);
  not not_3 (not_3_out, PC_IN[2]);
  and and_7 (and_7_out, CU_CONTROL, PC_IN[3]);
  and and_8 (and_8_out, CU_CONTROL, not_4_out);
  not not_4 (not_4_out, PC_IN[3]);
  S_R_Flip_Flop s_r_ff_1 (.S(and_1_out), .R(and_2_out), .clk(CLK), .Q(ADDR_OUT[0]));  // open: reset, Qn, preset
  S_R_Flip_Flop s_r_ff_2 (.S(and_3_out), .R(and_4_out), .clk(CLK), .Q(ADDR_OUT[1]));  // open: reset, Qn, preset
  S_R_Flip_Flop s_r_ff_3 (.S(and_5_out), .R(and_6_out), .clk(CLK), .Q(ADDR_OUT[2]));  // open: reset, Qn, preset
  S_R_Flip_Flop s_r_ff_4 (.S(and_7_out), .R(and_8_out), .clk(CLK), .Q(ADDR_OUT[3]));  // open: reset, Qn, preset

  assign out_4 = ADDR_OUT;
endmodule

module inputbuffer (
  input  CLK,
  input  one,
  input  two,
  input  three,
  input  four,
  input  five,
  input  six,
  input  seven,
  input  eight,
  input  nine,
  input  zero,
  input  RW,
  output [7:0] out_13,
  output [7:0] out_14
);

  wire and_1_out, and_2_out, and_3_out, and_4_out, and_5_out, and_6_out, and_7_out, and_8_out, and_9_out,
       and_10_out, and_11_out, and_12_out, and_13_out, and_14_out, and_15_out, and_16_out, not_1_out,
       not_2_out, not_3_out, not_4_out, not_5_out, not_6_out, not_7_out, not_8_out, not_9_out, not_10_out,
       or_1_out, or_2_out, or_3_out, or_4_out;

  or or_1 (or_1_out, one, three, five, seven, nine);
  or or_2 (or_2_out, two, three, six, seven);
  or or_3 (or_3_out, four, five, seven, six);
  or or_4 (or_4_out, eight, nine);
  not not_1 (not_1_out, or_1_out);
  not not_2 (not_2_out, or_2_out);
  not not_3 (not_3_out, or_3_out);
  not not_4 (not_4_out, or_4_out);
  not not_5 (not_5_out, 1'b0);
  not not_6 (not_6_out, 1'b0);
  not not_7 (not_7_out, 1'b0);
  not not_8 (not_8_out, not_10_out);
  not not_9 (not_9_out, 1'b0);
  not not_10 (not_10_out, RW);
  and and_1 (and_1_out, not_8_out, or_1_out);
  S_R_Flip_Flop s_r_ff_1 (.S(and_1_out), .R(and_2_out), .clk(CLK), .Q(out_13[0]));  // open: reset, Qn, preset
  and and_2 (and_2_out, not_8_out, not_1_out);
  S_R_Flip_Flop s_r_ff_2 (.S(and_3_out), .R(and_4_out), .clk(CLK), .Q(out_13[1]));  // open: reset, Qn, preset
  and and_3 (and_3_out, not_8_out, or_2_out);
  and and_4 (and_4_out, not_8_out, not_2_out);
  and and_5 (and_5_out, not_8_out, or_3_out);
  S_R_Flip_Flop s_r_ff_3 (.S(and_5_out), .R(and_6_out), .clk(CLK), .Q(out_13[2]));  // open: reset, Qn, preset
  and and_6 (and_6_out, not_8_out, not_3_out);
  and and_7 (and_7_out, not_8_out, or_4_out);
  S_R_Flip_Flop s_r_ff_4 (.S(and_7_out), .R(and_8_out), .clk(CLK), .Q(out_13[3]));  // open: reset, Qn, preset
  and and_8 (and_8_out, not_8_out, not_4_out);
  and and_9 (and_9_out, not_8_out, 1'b0);
  S_R_Flip_Flop s_r_ff_5 (.S(and_9_out), .R(and_10_out), .clk(CLK), .Q(out_13[4]));  // open: reset, Qn, preset
  and and_10 (and_10_out, not_8_out, not_5_out);
  and and_11 (and_11_out, not_8_out, 1'b0);
  S_R_Flip_Flop s_r_ff_6 (.S(and_11_out), .R(and_12_out), .clk(CLK), .Q(out_13[5]));  // open: reset, Qn, preset
  and and_12 (and_12_out, not_8_out, not_6_out);
  and and_13 (and_13_out, not_8_out, 1'b0);
  S_R_Flip_Flop s_r_ff_7 (.S(and_13_out), .R(and_14_out), .clk(CLK), .Q(out_13[6]));  // open: reset, Qn, preset
  and and_14 (and_14_out, not_8_out, not_7_out);
  and and_15 (and_15_out, not_8_out, 1'b0);
  S_R_Flip_Flop s_r_ff_8 (.S(and_15_out), .R(and_16_out), .clk(CLK), .Q(out_13[7]));  // open: reset, Qn, preset
  and and_16 (and_16_out, not_8_out, not_9_out);
  and and_17 (out_14[3], out_13[3], not_10_out);
  and and_18 (out_14[4], out_13[4], not_10_out);
  and and_19 (out_14[5], out_13[5], not_10_out);
  and and_20 (out_14[6], out_13[6], not_10_out);
  and and_21 (out_14[7], out_13[7], not_10_out);
  // Probe on out_13
  and and_22 (out_14[0], out_13[0], not_10_out);
  and and_23 (out_14[1], out_13[1], not_10_out);
  and and_24 (out_14[2], out_13[2], not_10_out);

  // Notes on the sheet:
  //   Data register
endmodule

module hexadigit (
  input  [3:0] in_1,
  output out_2,
  output out_3,
  output out_4,
  output out_5,
  output out_6,
  output out_7,
  output out_8
);

  wire A1_out, B1_out, C1_out, D1_out, E1_out, eleven_out, F1_out, fifthteen_out, five_out, four_out,
       fourteen_out, G1_out, nine_out, not_8_out, not_9_out, not_10_out, not_11_out, not_12_out, not_13_out,
       not_14_out, not_15_out, not_16_out, not_17_out, not_18_out, not_19_out, not_20_out, not_21_out,
       not_22_out, not_23_out, not_24_out, not_25_out, not_26_out, not_27_out, not_28_out, not_29_out,
       not_30_out, not_31_out, not_32_out, not_33_out, not_34_out, not_35_out, not_36_out, not_37_out,
       not_38_out, not_39_out, one_out, seven_out, six_out, ten_out, thirteen_out, three_out, twelve_out,
       two_out, Zero_out;

  not not_1 (out_2, A1_out);
  or A1 (A1_out, one_out, four_out, eleven_out, thirteen_out);
  not not_2 (out_3, B1_out);
  or B1 (B1_out, twelve_out, eleven_out, five_out, six_out, fourteen_out, fifthteen_out);
  or C1 (C1_out, fourteen_out, twelve_out, two_out, fifthteen_out);
  not not_3 (out_4, C1_out);
  not not_4 (out_5, D1_out);
  or D1 (D1_out, fifthteen_out, nine_out, one_out, four_out, seven_out, ten_out);
  not not_5 (out_6, E1_out);
  or E1 (E1_out, nine_out, three_out, one_out, four_out, five_out, seven_out);
  or F1 (F1_out, two_out, one_out, three_out, seven_out, thirteen_out);
  not not_6 (out_7, F1_out);
  not not_7 (out_8, G1_out);
  or G1 (G1_out, Zero_out, one_out, seven_out, twelve_out);
  not not_8 (not_8_out, in_1[2]);
  not not_9 (not_9_out, in_1[3]);
  not not_10 (not_10_out, in_1[1]);
  not not_11 (not_11_out, in_1[3]);
  not not_12 (not_12_out, in_1[0]);
  and Zero (Zero_out, not_11_out, not_8_out, not_10_out, not_12_out);
  not not_13 (not_13_out, in_1[2]);
  not not_14 (not_14_out, in_1[2]);
  not not_15 (not_15_out, in_1[3]);
  not not_16 (not_16_out, in_1[1]);
  and two (two_out, not_15_out, not_13_out, in_1[1], not_19_out);
  and one (one_out, not_9_out, not_14_out, not_16_out, in_1[0]);
  not not_17 (not_17_out, in_1[3]);
  not not_18 (not_18_out, in_1[2]);
  not not_19 (not_19_out, in_1[0]);
  and three (three_out, not_17_out, not_18_out, in_1[1], in_1[0]);
  not not_20 (not_20_out, in_1[3]);
  not not_21 (not_21_out, in_1[3]);
  not not_22 (not_22_out, in_1[1]);
  not not_23 (not_23_out, in_1[0]);
  and four (four_out, not_21_out, in_1[2], not_22_out, not_23_out);
  not not_24 (not_24_out, in_1[3]);
  not not_25 (not_25_out, in_1[1]);
  and six (six_out, not_24_out, in_1[2], in_1[1], not_27_out);
  and five (five_out, not_20_out, in_1[2], not_25_out, in_1[0]);
  not not_26 (not_26_out, in_1[3]);
  not not_27 (not_27_out, in_1[0]);
  and seven (seven_out, not_26_out, in_1[2], in_1[1], in_1[0]);
  not not_28 (not_28_out, in_1[1]);
  not not_29 (not_29_out, in_1[0]);
  not not_30 (not_30_out, in_1[2]);
  // AND_Gate eight has open pins: in0=in_1[3], in1=not_30_out, in2=not_28_out, in3=not_29_out, out=open
  not not_31 (not_31_out, in_1[1]);
  not not_32 (not_32_out, in_1[2]);
  not not_33 (not_33_out, in_1[2]);
  and nine (nine_out, in_1[3], not_33_out, not_31_out, in_1[0]);
  and ten (ten_out, in_1[3], not_32_out, in_1[1], not_35_out);
  not not_34 (not_34_out, in_1[2]);
  not not_35 (not_35_out, in_1[0]);
  and eleven (eleven_out, in_1[3], not_34_out, in_1[1], in_1[0]);
  not not_36 (not_36_out, in_1[1]);
  not not_37 (not_37_out, in_1[0]);
  and twelve (twelve_out, in_1[3], in_1[2], not_36_out, not_37_out);
  not not_38 (not_38_out, in_1[1]);
  and fourteen (fourteen_out, in_1[3], in_1[2], in_1[1], not_39_out);
  and thirteen (thirteen_out, in_1[3], in_1[2], not_38_out, in_1[0]);
  not not_39 (not_39_out, in_1[0]);
  and fifthteen (fifthteen_out, in_1[3], in_1[2], in_1[1], in_1[0]);
endmodule

module multiply_ALU (
  input  [7:0] \const ,
  input  [7:0] regnumber,
  output [7:0] out_put,
  output overflow_error
);

  wire fadder_1_cout, fadder_1_sum, fadder_2_cout, fadder_2_sum, fadder_3_cout, fadder_3_sum, fadder_4_cout,
       fadder_4_sum, fadder_5_cout, fadder_5_sum, fadder_6_cout, fadder_6_sum, fadder_7_cout, fadder_7_sum,
       fadder_8_cout, fadder_8_sum, fadder_9_cout, fadder_9_sum, fadder_10_cout, fadder_10_sum,
       fadder_11_sum, fadder_12_cout, fadder_12_sum, fadder_13_cout, fadder_13_sum, fadder_14_cout,
       fadder_14_sum, fadder_15_cout, fadder_15_sum, fadder_16_cout, fadder_16_sum, fadder_17_cout,
       fadder_17_sum, fadder_18_cout, fadder_18_sum, fadder_19_cout, fadder_19_sum, fadder_20_cout,
       fadder_20_sum, fadder_21_cout, fadder_21_sum, fadder_22_sum, fadder_23_cout, fadder_24_cout,
       fadder_25_cout, fadder_26_cout, fadder_27_cout, fadder_28_cout, fadder_29_cout, fadder_30_cout,
       fadder_31_cout, fadder_31_sum, fadder_32_cout, fadder_32_sum, fadder_33_sum;
  wire [7:0] multiplexer_1_out, multiplexer_2_out, multiplexer_3_out, multiplexer_4_out;

  Multiplexer #(.width(8), .enable("false")) multiplexer_1 (
    .in0({8{1'b0}}), .in1(regnumber), .out(multiplexer_1_out), .sel(\const [0]));
  Multiplexer #(.width(8), .enable("false")) multiplexer_2 (
    .in0({8{1'b0}}), .in1(regnumber), .out(multiplexer_2_out), .sel(\const [1]));
  Fadder fadder_1 (.Cin(1'b0), .A(1'b0), .B(multiplexer_1_out[0]), .Sum(fadder_1_sum), .Cout(fadder_1_cout));
  Fadder fadder_2 (
    .Cin(fadder_1_cout), .A(multiplexer_2_out[0]), .B(multiplexer_1_out[1]), .Sum(fadder_2_sum),
    .Cout(fadder_2_cout));
  Fadder fadder_3 (
    .Cin(fadder_2_cout), .A(multiplexer_2_out[1]), .B(multiplexer_1_out[2]), .Sum(fadder_3_sum),
    .Cout(fadder_3_cout));
  Fadder fadder_4 (
    .Cin(fadder_3_cout), .A(multiplexer_2_out[2]), .B(multiplexer_1_out[3]), .Sum(fadder_4_sum),
    .Cout(fadder_4_cout));
  Fadder fadder_5 (
    .Cin(fadder_4_cout), .A(multiplexer_2_out[3]), .B(multiplexer_1_out[4]), .Sum(fadder_5_sum),
    .Cout(fadder_5_cout));
  Fadder fadder_6 (
    .Cin(fadder_5_cout), .A(multiplexer_2_out[4]), .B(multiplexer_1_out[5]), .Sum(fadder_6_sum),
    .Cout(fadder_6_cout));
  Fadder fadder_7 (
    .Cin(fadder_6_cout), .A(multiplexer_2_out[5]), .B(multiplexer_1_out[6]), .Sum(fadder_7_sum),
    .Cout(fadder_7_cout));
  Fadder fadder_8 (
    .Cin(fadder_7_cout), .A(multiplexer_2_out[6]), .B(multiplexer_1_out[7]), .Sum(fadder_8_sum),
    .Cout(fadder_8_cout));
  Fadder fadder_9 (.Cin(fadder_8_cout), .A(multiplexer_2_out[7]), .B(1'b0), .Sum(fadder_9_sum), .Cout(fadder_9_cout));
  Fadder fadder_10 (.Cin(fadder_9_cout), .A(1'b0), .B(1'b0), .Sum(fadder_10_sum), .Cout(fadder_10_cout));
  Fadder fadder_11 (.Cin(fadder_10_cout), .A(1'b0), .B(1'b0), .Sum(fadder_11_sum));  // open: Cout
  Multiplexer #(.width(8), .enable("false")) multiplexer_3 (
    .in0({8{1'b0}}), .in1(regnumber), .out(multiplexer_3_out), .sel(\const [2]));
  Fadder fadder_12 (.Cin(1'b0), .A(1'b0), .B(fadder_1_sum), .Sum(fadder_12_sum), .Cout(fadder_12_cout));
  Fadder fadder_13 (.Cin(fadder_12_cout), .A(1'b0), .B(fadder_2_sum), .Sum(fadder_13_sum), .Cout(fadder_13_cout));
  Fadder fadder_14 (
    .Cin(fadder_13_cout), .A(multiplexer_3_out[0]), .B(fadder_3_sum), .Sum(fadder_14_sum),
    .Cout(fadder_14_cout));
  Fadder fadder_15 (
    .Cin(fadder_14_cout), .A(multiplexer_3_out[1]), .B(fadder_4_sum), .Sum(fadder_15_sum),
    .Cout(fadder_15_cout));
  Fadder fadder_16 (
    .Cin(fadder_15_cout), .A(multiplexer_3_out[2]), .B(fadder_5_sum), .Sum(fadder_16_sum),
    .Cout(fadder_16_cout));
  Fadder fadder_17 (
    .Cin(fadder_16_cout), .A(multiplexer_3_out[3]), .B(fadder_6_sum), .Sum(fadder_17_sum),
    .Cout(fadder_17_cout));
  Fadder fadder_18 (
    .Cin(fadder_17_cout), .A(multiplexer_3_out[4]), .B(fadder_7_sum), .Sum(fadder_18_sum),
    .Cout(fadder_18_cout));
  Fadder fadder_19 (
    .Cin(fadder_18_cout), .A(multiplexer_3_out[5]), .B(fadder_8_sum), .Sum(fadder_19_sum),
    .Cout(fadder_19_cout));
  Fadder fadder_20 (
    .Cin(fadder_19_cout), .A(multiplexer_3_out[6]), .B(fadder_9_sum), .Sum(fadder_20_sum),
    .Cout(fadder_20_cout));
  Fadder fadder_21 (
    .Cin(fadder_20_cout), .A(multiplexer_3_out[7]), .B(fadder_10_sum), .Sum(fadder_21_sum),
    .Cout(fadder_21_cout));
  Fadder fadder_22 (.Cin(fadder_21_cout), .A(1'b0), .B(fadder_11_sum), .Sum(fadder_22_sum));  // open: Cout
  Multiplexer #(.width(8), .enable("false")) multiplexer_4 (
    .in0({8{1'b0}}), .in1(regnumber), .out(multiplexer_4_out), .sel(\const [3]));
  Fadder fadder_23 (.A(1'b0), .B(fadder_12_sum), .Sum(out_put[0]), .Cout(fadder_23_cout));  // open: Cin
  Fadder fadder_24 (.Cin(fadder_23_cout), .A(1'b0), .B(fadder_13_sum), .Sum(out_put[1]), .Cout(fadder_24_cout));
  Fadder fadder_25 (.Cin(fadder_24_cout), .A(1'b0), .B(fadder_14_sum), .Sum(out_put[2]), .Cout(fadder_25_cout));
  Fadder fadder_26 (
    .Cin(fadder_25_cout), .A(multiplexer_4_out[0]), .B(fadder_15_sum), .Sum(out_put[3]), .Cout(fadder_26_cout));
  Fadder fadder_27 (
    .Cin(fadder_26_cout), .A(multiplexer_4_out[1]), .B(fadder_16_sum), .Sum(out_put[4]), .Cout(fadder_27_cout));
  Fadder fadder_28 (
    .Cin(fadder_27_cout), .A(multiplexer_4_out[2]), .B(fadder_17_sum), .Sum(out_put[5]), .Cout(fadder_28_cout));
  Fadder fadder_29 (
    .Cin(fadder_28_cout), .A(multiplexer_4_out[3]), .B(fadder_18_sum), .Sum(out_put[6]), .Cout(fadder_29_cout));
  Fadder fadder_30 (
    .Cin(fadder_29_cout), .A(multiplexer_4_out[4]), .B(fadder_19_sum), .Sum(out_put[7]), .Cout(fadder_30_cout));
  Fadder fadder_31 (
    .Cin(fadder_30_cout), .A(multiplexer_4_out[5]), .B(fadder_20_sum), .Sum(fadder_31_sum),
    .Cout(fadder_31_cout));
  Fadder fadder_32 (
    .Cin(fadder_31_cout), .A(multiplexer_4_out[6]), .B(fadder_21_sum), .Sum(fadder_32_sum),
    .Cout(fadder_32_cout));
  Fadder fadder_33 (
    .Cin(fadder_32_cout), .A(multiplexer_4_out[7]), .B(fadder_22_sum), .Sum(fadder_33_sum));  // open: Cout
  or or_1 (overflow_error, fadder_31_sum, fadder_32_sum, fadder_33_sum);
endmodule

module switch_to_decimal (
  input  [7:0] in_1,
  output [11:0] out_2
);

  wire and_1_out, and_2_out, and_3_out, and_4_out, and_5_out, and_6_out, and_7_out, and_8_out, and_9_out,
       and_10_out, and_11_out, and_12_out, and_13_out, and_14_out, and_15_out, and_16_out, and_17_out,
       and_18_out, and_19_out, and_20_out, and_21_out, and_22_out, and_23_out, and_24_out, and_25_out,
       and_26_out, and_27_out, and_28_out, and_29_out, and_30_out, and_31_out, and_32_out, fadder_1_cout,
       fadder_1_sum, fadder_2_cout, fadder_2_sum, fadder_3_cout, fadder_3_sum, fadder_4_cout, fadder_4_sum,
       fadder_5_cout, fadder_5_sum, fadder_6_cout, fadder_6_sum, fadder_7_cout, fadder_7_sum, fadder_8_cout,
       fadder_8_sum, fadder_9_cout, fadder_9_sum, fadder_10_cout, fadder_10_sum, fadder_11_cout,
       fadder_11_sum, fadder_12_cout, fadder_12_sum, fadder_13_cout, fadder_13_sum, fadder_14_cout,
       fadder_14_sum, fadder_15_cout, fadder_15_sum, fadder_16_cout, fadder_16_sum, fadder_17_cout,
       fadder_17_sum, fadder_18_cout, fadder_18_sum, fadder_19_cout, fadder_19_sum, fadder_20_cout,
       fadder_20_sum, fadder_21_cout, fadder_21_sum, fadder_22_cout, fadder_22_sum, fadder_23_cout,
       fadder_23_sum, fadder_24_cout, fadder_24_sum, fadder_25_cout, fadder_26_cout, fadder_27_cout,
       fadder_28_cout, fadder_29_cout, fadder_30_cout, fadder_31_cout, fadder_32_cout, fadder_33_cout,
       fadder_34_cout, or_1_out, or_2_out, or_3_out, or_4_out, or_5_out, or_6_out, or_7_out, or_8_out;

  and and_1 (and_1_out, in_1[6], in_1[7]);
  or or_1 (or_1_out, and_1_out, and_2_out);
  and and_2 (and_2_out, in_1[5], in_1[7]);
  Fadder fadder_1 (.Cin(1'b0), .A(in_1[5]), .B(and_3_out), .Sum(fadder_1_sum), .Cout(fadder_1_cout));
  and and_3 (and_3_out, or_1_out, 1'b1);
  Fadder fadder_2 (.Cin(fadder_1_cout), .A(in_1[6]), .B(and_4_out), .Sum(fadder_2_sum), .Cout(fadder_2_cout));
  and and_4 (and_4_out, or_1_out, 1'b1);
  Fadder fadder_3 (.Cin(fadder_2_cout), .A(in_1[7]), .B(1'b0), .Sum(fadder_3_sum), .Cout(fadder_3_cout));
  and and_5 (and_5_out, in_1[4], fadder_2_sum);
  and and_6 (and_6_out, fadder_1_sum, fadder_2_sum);
  Fadder fadder_4 (.Cin(1'b0), .A(in_1[4]), .B(and_7_out), .Sum(fadder_4_sum), .Cout(fadder_4_cout));
  and and_7 (and_7_out, or_2_out, 1'b1);
  or or_2 (or_2_out, and_5_out, fadder_3_sum, and_6_out);
  Fadder fadder_5 (.Cin(fadder_4_cout), .A(fadder_1_sum), .B(and_8_out), .Sum(fadder_5_sum), .Cout(fadder_5_cout));
  and and_8 (and_8_out, or_2_out, 1'b1);
  Fadder fadder_6 (.Cin(fadder_5_cout), .A(fadder_2_sum), .B(1'b0), .Sum(fadder_6_sum), .Cout(fadder_6_cout));
  Fadder fadder_7 (.Cin(fadder_6_cout), .A(fadder_3_sum), .B(1'b0), .Sum(fadder_7_sum), .Cout(fadder_7_cout));
  Fadder fadder_8 (.Cin(fadder_7_cout), .A(fadder_3_cout), .B(1'b0), .Sum(fadder_8_sum), .Cout(fadder_8_cout));
  and and_9 (and_9_out, in_1[3], fadder_5_sum);
  and and_10 (and_10_out, fadder_7_sum, fadder_8_cout);
  and and_11 (and_11_out, fadder_4_sum, fadder_5_sum);
  and and_12 (and_12_out, fadder_8_sum, fadder_8_cout);
  Fadder fadder_9 (.Cin(1'b0), .A(in_1[3]), .B(and_13_out), .Sum(fadder_9_sum), .Cout(fadder_9_cout));
  and and_13 (and_13_out, or_3_out, 1'b1);
  or or_3 (or_3_out, and_9_out, fadder_6_sum, and_11_out);
  Fadder fadder_10 (.Cin(fadder_9_cout), .A(fadder_4_sum), .B(and_14_out), .Sum(fadder_10_sum), .Cout(fadder_10_cout));
  and and_14 (and_14_out, or_3_out, 1'b1);
  Fadder fadder_11 (.Cin(fadder_10_cout), .A(fadder_5_sum), .B(1'b0), .Sum(fadder_11_sum), .Cout(fadder_11_cout));
  Fadder fadder_12 (.Cin(fadder_11_cout), .A(fadder_6_sum), .B(1'b0), .Sum(fadder_12_sum), .Cout(fadder_12_cout));
  Fadder fadder_13 (.Cin(fadder_12_cout), .A(fadder_7_sum), .B(and_15_out), .Sum(fadder_13_sum), .Cout(fadder_13_cout));
  and and_15 (and_15_out, or_4_out, 1'b1);
  or or_4 (or_4_out, and_10_out, and_12_out);
  Fadder fadder_14 (.Cin(fadder_13_cout), .A(fadder_8_sum), .B(and_16_out), .Sum(fadder_14_sum), .Cout(fadder_14_cout));
  and and_16 (and_16_out, or_4_out, 1'b1);
  Fadder fadder_15 (.Cin(fadder_14_cout), .A(fadder_8_cout), .B(1'b0), .Sum(fadder_15_sum), .Cout(fadder_15_cout));
  and and_17 (and_17_out, in_1[2], fadder_10_sum);
  and and_18 (and_18_out, fadder_12_sum, fadder_14_sum);
  and and_19 (and_19_out, fadder_9_sum, fadder_10_sum);
  and and_20 (and_20_out, fadder_13_sum, fadder_14_sum);
  Fadder fadder_16 (.Cin(1'b0), .A(in_1[2]), .B(and_21_out), .Sum(fadder_16_sum), .Cout(fadder_16_cout));
  and and_21 (and_21_out, or_5_out, 1'b1);
  or or_5 (or_5_out, and_17_out, fadder_11_sum, and_19_out);
  Fadder fadder_17 (.Cin(fadder_16_cout), .A(fadder_9_sum), .B(and_22_out), .Sum(fadder_17_sum), .Cout(fadder_17_cout));
  and and_22 (and_22_out, or_5_out, 1'b1);
  Fadder fadder_18 (.Cin(fadder_17_cout), .A(fadder_10_sum), .B(1'b0), .Sum(fadder_18_sum), .Cout(fadder_18_cout));
  Fadder fadder_19 (.Cin(fadder_18_cout), .A(fadder_11_sum), .B(1'b0), .Sum(fadder_19_sum), .Cout(fadder_19_cout));
  Fadder fadder_20 (
    .Cin(fadder_19_cout), .A(fadder_12_sum), .B(and_23_out), .Sum(fadder_20_sum), .Cout(fadder_20_cout));
  and and_23 (and_23_out, or_6_out, 1'b1);
  or or_6 (or_6_out, and_18_out, fadder_15_sum, and_20_out);
  Fadder fadder_21 (
    .Cin(fadder_20_cout), .A(fadder_13_sum), .B(and_24_out), .Sum(fadder_21_sum), .Cout(fadder_21_cout));
  and and_24 (and_24_out, or_6_out, 1'b1);
  Fadder fadder_22 (.Cin(fadder_21_cout), .A(fadder_14_sum), .B(1'b0), .Sum(fadder_22_sum), .Cout(fadder_22_cout));
  Fadder fadder_23 (.Cin(fadder_22_cout), .A(fadder_15_sum), .B(1'b0), .Sum(fadder_23_sum), .Cout(fadder_23_cout));
  Fadder fadder_24 (.Cin(fadder_23_cout), .A(fadder_15_cout), .B(1'b0), .Sum(fadder_24_sum), .Cout(fadder_24_cout));
  and and_25 (and_25_out, in_1[1], fadder_17_sum);
  and and_26 (and_26_out, fadder_19_sum, fadder_21_sum);
  and and_27 (and_27_out, fadder_16_sum, fadder_17_sum);
  and and_28 (and_28_out, fadder_20_sum, fadder_21_sum);
  Fadder fadder_25 (.Cin(1'b0), .A(in_1[1]), .B(and_29_out), .Sum(out_2[1]), .Cout(fadder_25_cout));
  and and_29 (and_29_out, or_7_out, 1'b1);
  or or_7 (or_7_out, and_25_out, fadder_18_sum, and_27_out);
  Fadder fadder_26 (.Cin(fadder_25_cout), .A(fadder_16_sum), .B(and_30_out), .Sum(out_2[2]), .Cout(fadder_26_cout));
  and and_30 (and_30_out, or_7_out, 1'b1);
  Fadder fadder_27 (.Cin(fadder_26_cout), .A(fadder_17_sum), .B(1'b0), .Sum(out_2[3]), .Cout(fadder_27_cout));
  Fadder fadder_28 (.Cin(fadder_27_cout), .A(fadder_18_sum), .B(1'b0), .Sum(out_2[4]), .Cout(fadder_28_cout));
  Fadder fadder_29 (.Cin(fadder_28_cout), .A(fadder_19_sum), .B(and_31_out), .Sum(out_2[5]), .Cout(fadder_29_cout));
  and and_31 (and_31_out, or_8_out, 1'b1);
  or or_8 (or_8_out, and_26_out, fadder_22_sum, and_28_out);
  Fadder fadder_30 (.Cin(fadder_29_cout), .A(fadder_20_sum), .B(and_32_out), .Sum(out_2[6]), .Cout(fadder_30_cout));
  and and_32 (and_32_out, or_8_out, 1'b1);
  Fadder fadder_31 (.Cin(fadder_30_cout), .A(fadder_21_sum), .B(1'b0), .Sum(out_2[7]), .Cout(fadder_31_cout));
  Fadder fadder_32 (.Cin(fadder_31_cout), .A(fadder_22_sum), .B(1'b0), .Sum(out_2[8]), .Cout(fadder_32_cout));
  Fadder fadder_33 (.Cin(fadder_32_cout), .A(fadder_23_sum), .B(1'b0), .Sum(out_2[9]), .Cout(fadder_33_cout));
  Fadder fadder_34 (.Cin(fadder_33_cout), .A(fadder_24_sum), .B(1'b0), .Sum(out_2[10]), .Cout(fadder_34_cout));
  Fadder fadder_35 (.Cin(fadder_34_cout), .A(fadder_24_cout), .B(1'b0), .Sum(out_2[11]));  // open: Cout

  assign out_2[0] = in_1[0];
endmodule
